// Logisim project 8_Bit_CPU.circ as structural Verilog: 40 circuits, main circuit main
module main (
  output [7:0] count,
  output carry
);

  wire clock_1_out, counter_1_carry, cpu_clk_1_clke;

  Clock clock_1 (.out(clock_1_out));
  CPU_CLK cpu_clk_1 (.clkin(clock_1_out), .clke(cpu_clk_1_clke));  // open: clks, clk
  Counter #(.ongoal("stay"), .trigger("falling")) counter_1 (
    .count(cpu_clk_1_clke), .Q(count), .carry(counter_1_carry), .clk(1'b1));  // open: load, D, clr
  not not_1 (carry, counter_1_carry);
endmodule

module CPU_MEM_1 (
  input  in_1,
  input  in_2,
  output out_3
);

  wire nand_1_out, nand_2_out, nand_4_out;

  nand nand_1 (nand_1_out, in_1, in_2);
  nand nand_2 (nand_2_out, nand_1_out, in_2);
  nand nand_3 (out_3, nand_1_out, nand_4_out);
  nand nand_4 (nand_4_out, out_3, nand_2_out);

  // Notes on the sheet:
  //   in_2: pull=down
  //   out_3: pull=up
  //   in_1: pull=down
endmodule

module CPU_MEM_8 (
  input  [7:0] in_1,
  input  s,
  output [7:0] out_3
);

  CPU_MEM_1 cpu_mem_1_1 (.in_1(in_1[0]), .in_2(s), .out_3(out_3[0]));
  CPU_MEM_1 cpu_mem_1_2 (.in_1(in_1[1]), .in_2(s), .out_3(out_3[1]));
  CPU_MEM_1 cpu_mem_1_3 (.in_1(in_1[2]), .in_2(s), .out_3(out_3[2]));
  CPU_MEM_1 cpu_mem_1_4 (.in_1(in_1[3]), .in_2(s), .out_3(out_3[3]));
  CPU_MEM_1 cpu_mem_1_5 (.in_1(in_1[4]), .in_2(s), .out_3(out_3[4]));
  CPU_MEM_1 cpu_mem_1_6 (.in_1(in_1[5]), .in_2(s), .out_3(out_3[5]));
  CPU_MEM_1 cpu_mem_1_7 (.in_1(in_1[6]), .in_2(s), .out_3(out_3[6]));
  CPU_MEM_1 cpu_mem_1_8 (.in_1(in_1[7]), .in_2(s), .out_3(out_3[7]));

  // Notes on the sheet:
  //   in_1: pull=down
  //   out_3: pull=down
  //   s: pull=down
endmodule

module CPU_ENABLE_8 (
  input  [7:0] in_1,
  input  in_2,
  output [7:0] out_3
);

  wire and_1_out, and_2_out, and_3_out, and_4_out, and_5_out, and_6_out, and_7_out, and_8_out;

  and and_1 (and_1_out, in_1[0], in_2);
  assign out_3[0] = in_2 ? and_1_out : 1'bz;  // Controlled_Buffer controlled_buffer_1
  assign out_3[1] = in_2 ? and_2_out : 1'bz;  // Controlled_Buffer controlled_buffer_2
  and and_2 (and_2_out, in_1[1], in_2);
  and and_3 (and_3_out, in_1[2], in_2);
  assign out_3[2] = in_2 ? and_3_out : 1'bz;  // Controlled_Buffer controlled_buffer_3
  and and_4 (and_4_out, in_1[3], in_2);
  assign out_3[3] = in_2 ? and_4_out : 1'bz;  // Controlled_Buffer controlled_buffer_4
  assign out_3[4] = in_2 ? and_5_out : 1'bz;  // Controlled_Buffer controlled_buffer_5
  and and_5 (and_5_out, in_1[4], in_2);
  and and_6 (and_6_out, in_1[5], in_2);
  assign out_3[5] = in_2 ? and_6_out : 1'bz;  // Controlled_Buffer controlled_buffer_6
  assign out_3[6] = in_2 ? and_7_out : 1'bz;  // Controlled_Buffer controlled_buffer_7
  and and_7 (and_7_out, in_1[6], in_2);
  and and_8 (and_8_out, in_1[7], in_2);
  assign out_3[7] = in_2 ? and_8_out : 1'bz;  // Controlled_Buffer controlled_buffer_8
endmodule

module CPU_REGISTER_8 (
  input  [7:0] i,
  input  s,
  input  e,
  output [7:0] REG,
  output [7:0] _0
);

  wire [7:0] cpu_enable_8_1_out_3;

  CPU_MEM_8 cpu_mem_8_1 (.s(s), .in_1(i), .out_3(REG));
  CPU_ENABLE_8 cpu_enable_8_1 (.in_1(REG), .out_3(cpu_enable_8_1_out_3), .in_2(e));
  assign _0 = e ? cpu_enable_8_1_out_3 : 8'bz;  // Controlled_Buffer controlled_buffer_1

  // Notes on the sheet:
  //   _0: pull=down
  //   i: pull=down
  //   s: pull=down
  //   e: pull=down
endmodule

module CPU_DECODER_4x16 (
  input  [3:0] in_1,
  output L,
  output out_3,
  output out_4,
  output out_5,
  output out_6,
  output out_7,
  output out_8,
  output out_9,
  output out_10,
  output out_11,
  output out_12,
  output out_13,
  output out_14,
  output out_15,
  output out_16,
  output M
);

  wire not_1_out, not_2_out, not_3_out, not_4_out;

  not not_1 (not_1_out, in_1[0]);
  not not_2 (not_2_out, in_1[1]);
  not not_3 (not_3_out, in_1[2]);
  not not_4 (not_4_out, in_1[3]);
  and and_1 (L, not_4_out, not_3_out, not_2_out, not_1_out);
  and and_2 (out_3, not_4_out, not_3_out, not_2_out, in_1[0]);
  and and_3 (out_4, not_4_out, not_3_out, in_1[1], not_1_out);
  and and_4 (out_5, not_4_out, not_3_out, in_1[1], in_1[0]);
  and and_5 (out_6, not_4_out, in_1[2], not_2_out, not_1_out);
  and and_6 (out_7, not_4_out, in_1[2], not_2_out, in_1[0]);
  and and_7 (out_8, not_4_out, in_1[2], in_1[1], not_1_out);
  and and_8 (out_9, not_4_out, in_1[2], in_1[1], in_1[0]);
  and and_9 (out_10, in_1[3], not_3_out, not_2_out, not_1_out);
  and and_10 (out_11, in_1[3], not_3_out, not_2_out, in_1[0]);
  and and_11 (out_12, in_1[3], not_3_out, in_1[1], not_1_out);
  and and_12 (out_13, in_1[3], not_3_out, in_1[1], in_1[0]);
  and and_13 (out_14, in_1[3], in_1[2], not_2_out, not_1_out);
  and and_14 (out_15, in_1[3], in_1[2], not_2_out, in_1[0]);
  and and_15 (out_16, in_1[3], in_1[2], in_1[1], not_1_out);
  and and_16 (M, in_1[3], in_1[2], in_1[1], in_1[0]);

  // Notes on the sheet:
  //   out_11: pull=down
  //   out_3: pull=down
  //   out_12: pull=down
  //   out_14: pull=down
  //   out_6: pull=down
  //   out_8: pull=down
  //   out_9: pull=down
  //   out_16: pull=down
  //   out_5: pull=down
  //   M: pull=down
  //   out_15: pull=down
  //   L: pull=down
  //   out_13: pull=down
  //   in_1: pull=down
  //   out_7: pull=down
  //   out_4: pull=down
  //   out_10: pull=down
endmodule

module CPU_REG_BYTE (
  input  [7:0] i,
  input  RESET,
  input  h,
  input  v,
  input  s,
  input  e,
  output [7:0] o,
  output [7:0] op
);

  wire and_1_out, and_2_out, and_3_out, or_1_out;
  wire [7:0] cpu_register_8_1__0;

  and and_1 (and_1_out, h, v);
  and and_2 (and_2_out, and_1_out, s);
  and and_3 (and_3_out, and_1_out, e);
  or or_1 (or_1_out, RESET, and_2_out);
  CPU_REGISTER_8 cpu_register_8_1 (.i(i), .s(or_1_out), .e(and_3_out), ._0(cpu_register_8_1__0), .REG(op));
  assign o = and_3_out ? cpu_register_8_1__0 : 8'bz;  // Controlled_Buffer controlled_buffer_1

  // Notes on the sheet:
  //   RESET: pull=down
  //   i: pull=down
  //   o: pull=down
  //   e: pull=down
  //   op: pull=down
  //   v: pull=down
  //   s: pull=down
  //   h: pull=down
endmodule

module CPU_RAM_256 (
  input  reset,
  input  [7:0] i,
  input  sa,
  input  [7:0] address,
  input  s,
  input  e,
  output [7:0] o,
  output [7:0] _15,
  output [7:0] _14,
  output [7:0] _13,
  output [7:0] _12,
  output [7:0] _11,
  output [7:0] _10,
  output [7:0] _9,
  output [7:0] _8,
  output [7:0] _7,
  output [7:0] _6,
  output [7:0] _5,
  output [7:0] _4,
  output [7:0] _3,
  output [7:0] _2,
  output [7:0] _1,
  output [7:0] _0,
  output [7:0] _31,
  output [7:0] _30,
  output [7:0] _29,
  output [7:0] _28,
  output [7:0] _27,
  output [7:0] _26,
  output [7:0] _25,
  output [7:0] _24,
  output [7:0] _23,
  output [7:0] _22,
  output [7:0] _21,
  output [7:0] _20,
  output [7:0] _19,
  output [7:0] _18,
  output [7:0] _17,
  output [7:0] _16,
  output [7:0] _47,
  output [7:0] _46,
  output [7:0] _45,
  output [7:0] _44,
  output [7:0] _43,
  output [7:0] _42,
  output [7:0] _41,
  output [7:0] _40,
  output [7:0] _39,
  output [7:0] _38,
  output [7:0] _37,
  output [7:0] _36,
  output [7:0] _35,
  output [7:0] _34,
  output [7:0] _33,
  output [7:0] _32,
  output [7:0] _63,
  output [7:0] _62,
  output [7:0] _61,
  output [7:0] _60,
  output [7:0] _59,
  output [7:0] _58,
  output [7:0] _57,
  output [7:0] _56,
  output [7:0] _55,
  output [7:0] _54,
  output [7:0] _53,
  output [7:0] _52,
  output [7:0] _51,
  output [7:0] _50,
  output [7:0] _49,
  output [7:0] _48,
  output [7:0] _79,
  output [7:0] _78,
  output [7:0] _77,
  output [7:0] _76,
  output [7:0] _75,
  output [7:0] _74,
  output [7:0] _73,
  output [7:0] _72,
  output [7:0] _71,
  output [7:0] _70,
  output [7:0] _69,
  output [7:0] _68,
  output [7:0] _67,
  output [7:0] _66,
  output [7:0] _65,
  output [7:0] _64,
  output [7:0] _95,
  output [7:0] _94,
  output [7:0] _93,
  output [7:0] _92,
  output [7:0] _91,
  output [7:0] _90,
  output [7:0] _89,
  output [7:0] _88,
  output [7:0] _87,
  output [7:0] _86,
  output [7:0] _85,
  output [7:0] _84,
  output [7:0] _83,
  output [7:0] _82,
  output [7:0] _81,
  output [7:0] _80,
  output [7:0] _111,
  output [7:0] _110,
  output [7:0] _109,
  output [7:0] _108,
  output [7:0] _107,
  output [7:0] _106,
  output [7:0] _105,
  output [7:0] _104,
  output [7:0] _103,
  output [7:0] _102,
  output [7:0] _101,
  output [7:0] _100,
  output [7:0] _99,
  output [7:0] _98,
  output [7:0] _97,
  output [7:0] _96,
  output [7:0] _127,
  output [7:0] _126,
  output [7:0] _125,
  output [7:0] _124,
  output [7:0] _123,
  output [7:0] _122,
  output [7:0] _121,
  output [7:0] _120,
  output [7:0] _119,
  output [7:0] _118,
  output [7:0] _117,
  output [7:0] _116,
  output [7:0] _115,
  output [7:0] _114,
  output [7:0] _113,
  output [7:0] _112,
  output [7:0] _143,
  output [7:0] _142,
  output [7:0] _141,
  output [7:0] _140,
  output [7:0] _139,
  output [7:0] _138,
  output [7:0] _137,
  output [7:0] _136,
  output [7:0] _135,
  output [7:0] _134,
  output [7:0] _133,
  output [7:0] _132,
  output [7:0] _131,
  output [7:0] _130,
  output [7:0] _129,
  output [7:0] _128,
  output [7:0] _159,
  output [7:0] _158,
  output [7:0] _157,
  output [7:0] _156,
  output [7:0] _155,
  output [7:0] _154,
  output [7:0] _153,
  output [7:0] _152,
  output [7:0] _151,
  output [7:0] _150,
  output [7:0] _149,
  output [7:0] _148,
  output [7:0] _147,
  output [7:0] _146,
  output [7:0] _145,
  output [7:0] _144,
  output [7:0] _175,
  output [7:0] _174,
  output [7:0] _173,
  output [7:0] _172,
  output [7:0] _171,
  output [7:0] _170,
  output [7:0] _169,
  output [7:0] _168,
  output [7:0] _167,
  output [7:0] _166,
  output [7:0] _165,
  output [7:0] _164,
  output [7:0] _163,
  output [7:0] _162,
  output [7:0] _161,
  output [7:0] _160,
  output [7:0] _191,
  output [7:0] _190,
  output [7:0] _189,
  output [7:0] _188,
  output [7:0] _187,
  output [7:0] _186,
  output [7:0] _185,
  output [7:0] _184,
  output [7:0] _183,
  output [7:0] _182,
  output [7:0] _181,
  output [7:0] _180,
  output [7:0] _179,
  output [7:0] _178,
  output [7:0] _177,
  output [7:0] _176,
  output [7:0] _207,
  output [7:0] _206,
  output [7:0] _205,
  output [7:0] _204,
  output [7:0] _203,
  output [7:0] _202,
  output [7:0] _201,
  output [7:0] _200,
  output [7:0] _199,
  output [7:0] _198,
  output [7:0] _197,
  output [7:0] _196,
  output [7:0] _195,
  output [7:0] _194,
  output [7:0] _193,
  output [7:0] _192,
  output [7:0] _223,
  output [7:0] _222,
  output [7:0] _221,
  output [7:0] _220,
  output [7:0] _219,
  output [7:0] _218,
  output [7:0] _217,
  output [7:0] _216,
  output [7:0] _215,
  output [7:0] _214,
  output [7:0] _213,
  output [7:0] _212,
  output [7:0] _211,
  output [7:0] _210,
  output [7:0] _209,
  output [7:0] _208,
  output [7:0] _239,
  output [7:0] _238,
  output [7:0] _237,
  output [7:0] _236,
  output [7:0] _235,
  output [7:0] _234,
  output [7:0] _233,
  output [7:0] _232,
  output [7:0] _231,
  output [7:0] _230,
  output [7:0] _229,
  output [7:0] _228,
  output [7:0] _227,
  output [7:0] _226,
  output [7:0] _225,
  output [7:0] _224,
  output [7:0] _255,
  output [7:0] _254,
  output [7:0] _253,
  output [7:0] _252,
  output [7:0] _251,
  output [7:0] _250,
  output [7:0] _249,
  output [7:0] _248,
  output [7:0] _247,
  output [7:0] _246,
  output [7:0] _245,
  output [7:0] _244,
  output [7:0] _243,
  output [7:0] _242,
  output [7:0] _241,
  output [7:0] _240
);

  wire cpu_decoder_4x16_1_l, cpu_decoder_4x16_1_m, cpu_decoder_4x16_1_out_3, cpu_decoder_4x16_1_out_4,
       cpu_decoder_4x16_1_out_5, cpu_decoder_4x16_1_out_6, cpu_decoder_4x16_1_out_7,
       cpu_decoder_4x16_1_out_8, cpu_decoder_4x16_1_out_9, cpu_decoder_4x16_1_out_10,
       cpu_decoder_4x16_1_out_11, cpu_decoder_4x16_1_out_12, cpu_decoder_4x16_1_out_13,
       cpu_decoder_4x16_1_out_14, cpu_decoder_4x16_1_out_15, cpu_decoder_4x16_1_out_16, cpu_decoder_4x16_2_l,
       cpu_decoder_4x16_2_m, cpu_decoder_4x16_2_out_3, cpu_decoder_4x16_2_out_4, cpu_decoder_4x16_2_out_5,
       cpu_decoder_4x16_2_out_6, cpu_decoder_4x16_2_out_7, cpu_decoder_4x16_2_out_8,
       cpu_decoder_4x16_2_out_9, cpu_decoder_4x16_2_out_10, cpu_decoder_4x16_2_out_11,
       cpu_decoder_4x16_2_out_12, cpu_decoder_4x16_2_out_13, cpu_decoder_4x16_2_out_14,
       cpu_decoder_4x16_2_out_15, cpu_decoder_4x16_2_out_16;
  wire [7:0] cpu_mem_8_1_out_3, cpu_reg_byte_1_o;

  CPU_MEM_8 cpu_mem_8_1 (.s(sa), .in_1(address), .out_3(cpu_mem_8_1_out_3));
  CPU_DECODER_4x16 cpu_decoder_4x16_1 (
    .in_1(cpu_mem_8_1_out_3[7:4]), .L(cpu_decoder_4x16_1_l), .out_3(cpu_decoder_4x16_1_out_3),
    .out_4(cpu_decoder_4x16_1_out_4), .out_5(cpu_decoder_4x16_1_out_5), .out_6(cpu_decoder_4x16_1_out_6),
    .out_7(cpu_decoder_4x16_1_out_7), .out_8(cpu_decoder_4x16_1_out_8), .out_9(cpu_decoder_4x16_1_out_9),
    .out_10(cpu_decoder_4x16_1_out_10), .out_11(cpu_decoder_4x16_1_out_11),
    .out_12(cpu_decoder_4x16_1_out_12), .out_13(cpu_decoder_4x16_1_out_13),
    .out_14(cpu_decoder_4x16_1_out_14), .out_15(cpu_decoder_4x16_1_out_15),
    .out_16(cpu_decoder_4x16_1_out_16), .M(cpu_decoder_4x16_1_m));
  assign o = e ? cpu_reg_byte_1_o : 8'bz;  // Controlled_Buffer controlled_buffer_1
  CPU_REG_BYTE cpu_reg_byte_1 (
    .h(cpu_decoder_4x16_1_l), .v(cpu_decoder_4x16_2_m), .i(i), .o(cpu_reg_byte_1_o), .s(s), .e(e),
    .RESET(reset), .op(_15));
  CPU_REG_BYTE cpu_reg_byte_2 (
    .h(cpu_decoder_4x16_1_out_3), .v(cpu_decoder_4x16_2_m), .i(i), .o(cpu_reg_byte_1_o), .s(s), .e(e),
    .RESET(reset), .op(_31));
  CPU_REG_BYTE cpu_reg_byte_3 (
    .h(cpu_decoder_4x16_1_out_4), .v(cpu_decoder_4x16_2_m), .i(i), .o(cpu_reg_byte_1_o), .s(s), .e(e),
    .RESET(reset), .op(_47));
  CPU_REG_BYTE cpu_reg_byte_4 (
    .h(cpu_decoder_4x16_1_out_5), .v(cpu_decoder_4x16_2_m), .i(i), .o(cpu_reg_byte_1_o), .s(s), .e(e),
    .RESET(reset), .op(_63));
  CPU_REG_BYTE cpu_reg_byte_5 (
    .h(cpu_decoder_4x16_1_out_6), .v(cpu_decoder_4x16_2_m), .i(i), .o(cpu_reg_byte_1_o), .s(s), .e(e),
    .RESET(reset), .op(_79));
  CPU_REG_BYTE cpu_reg_byte_6 (
    .h(cpu_decoder_4x16_1_out_7), .v(cpu_decoder_4x16_2_m), .i(i), .o(cpu_reg_byte_1_o), .s(s), .e(e),
    .RESET(reset), .op(_95));
  CPU_REG_BYTE cpu_reg_byte_7 (
    .h(cpu_decoder_4x16_1_out_8), .v(cpu_decoder_4x16_2_m), .i(i), .o(cpu_reg_byte_1_o), .s(s), .e(e),
    .RESET(reset), .op(_111));
  CPU_REG_BYTE cpu_reg_byte_8 (
    .h(cpu_decoder_4x16_1_out_9), .v(cpu_decoder_4x16_2_m), .i(i), .o(cpu_reg_byte_1_o), .s(s), .e(e),
    .RESET(reset), .op(_127));
  CPU_REG_BYTE cpu_reg_byte_9 (
    .h(cpu_decoder_4x16_1_out_10), .v(cpu_decoder_4x16_2_m), .i(i), .o(cpu_reg_byte_1_o), .s(s), .e(e),
    .RESET(reset), .op(_143));
  CPU_REG_BYTE cpu_reg_byte_10 (
    .h(cpu_decoder_4x16_1_out_11), .v(cpu_decoder_4x16_2_m), .i(i), .o(cpu_reg_byte_1_o), .s(s), .e(e),
    .RESET(reset), .op(_159));
  CPU_REG_BYTE cpu_reg_byte_11 (
    .h(cpu_decoder_4x16_1_out_12), .v(cpu_decoder_4x16_2_m), .i(i), .o(cpu_reg_byte_1_o), .s(s), .e(e),
    .RESET(reset), .op(_175));
  CPU_REG_BYTE cpu_reg_byte_12 (
    .h(cpu_decoder_4x16_1_out_13), .v(cpu_decoder_4x16_2_m), .i(i), .o(cpu_reg_byte_1_o), .s(s), .e(e),
    .RESET(reset), .op(_191));
  CPU_REG_BYTE cpu_reg_byte_13 (
    .h(cpu_decoder_4x16_1_out_14), .v(cpu_decoder_4x16_2_m), .i(i), .o(cpu_reg_byte_1_o), .s(s), .e(e),
    .RESET(reset), .op(_207));
  CPU_REG_BYTE cpu_reg_byte_14 (
    .h(cpu_decoder_4x16_1_out_15), .v(cpu_decoder_4x16_2_m), .i(i), .o(cpu_reg_byte_1_o), .s(s), .e(e),
    .RESET(reset), .op(_223));
  CPU_REG_BYTE cpu_reg_byte_15 (
    .h(cpu_decoder_4x16_1_out_16), .v(cpu_decoder_4x16_2_m), .i(i), .o(cpu_reg_byte_1_o), .s(s), .e(e),
    .RESET(reset), .op(_239));
  CPU_REG_BYTE cpu_reg_byte_16 (
    .h(cpu_decoder_4x16_1_m), .v(cpu_decoder_4x16_2_m), .i(i), .o(cpu_reg_byte_1_o), .s(s), .e(e),
    .RESET(reset), .op(_255));
  CPU_REG_BYTE cpu_reg_byte_17 (
    .h(cpu_decoder_4x16_1_l), .v(cpu_decoder_4x16_2_out_16), .i(i), .o(cpu_reg_byte_1_o), .s(s), .e(e),
    .RESET(reset), .op(_14));
  CPU_REG_BYTE cpu_reg_byte_18 (
    .h(cpu_decoder_4x16_1_out_3), .v(cpu_decoder_4x16_2_out_16), .i(i), .o(cpu_reg_byte_1_o), .s(s), .e(e),
    .RESET(reset), .op(_30));
  CPU_REG_BYTE cpu_reg_byte_19 (
    .h(cpu_decoder_4x16_1_out_4), .v(cpu_decoder_4x16_2_out_16), .i(i), .o(cpu_reg_byte_1_o), .s(s), .e(e),
    .RESET(reset), .op(_46));
  CPU_REG_BYTE cpu_reg_byte_20 (
    .h(cpu_decoder_4x16_1_out_5), .v(cpu_decoder_4x16_2_out_16), .i(i), .o(cpu_reg_byte_1_o), .s(s), .e(e),
    .RESET(reset), .op(_62));
  CPU_REG_BYTE cpu_reg_byte_21 (
    .h(cpu_decoder_4x16_1_out_6), .v(cpu_decoder_4x16_2_out_16), .i(i), .o(cpu_reg_byte_1_o), .s(s), .e(e),
    .RESET(reset), .op(_78));
  CPU_REG_BYTE cpu_reg_byte_22 (
    .h(cpu_decoder_4x16_1_out_7), .v(cpu_decoder_4x16_2_out_16), .i(i), .o(cpu_reg_byte_1_o), .s(s), .e(e),
    .RESET(reset), .op(_94));
  CPU_REG_BYTE cpu_reg_byte_23 (
    .h(cpu_decoder_4x16_1_out_8), .v(cpu_decoder_4x16_2_out_16), .i(i), .o(cpu_reg_byte_1_o), .s(s), .e(e),
    .RESET(reset), .op(_110));
  CPU_REG_BYTE cpu_reg_byte_24 (
    .h(cpu_decoder_4x16_1_out_9), .v(cpu_decoder_4x16_2_out_16), .i(i), .o(cpu_reg_byte_1_o), .s(s), .e(e),
    .RESET(reset), .op(_126));
  CPU_REG_BYTE cpu_reg_byte_25 (
    .h(cpu_decoder_4x16_1_out_10), .v(cpu_decoder_4x16_2_out_16), .i(i), .o(cpu_reg_byte_1_o), .s(s), .e(e),
    .RESET(reset), .op(_142));
  CPU_REG_BYTE cpu_reg_byte_26 (
    .h(cpu_decoder_4x16_1_out_11), .v(cpu_decoder_4x16_2_out_16), .i(i), .o(cpu_reg_byte_1_o), .s(s), .e(e),
    .RESET(reset), .op(_158));
  CPU_REG_BYTE cpu_reg_byte_27 (
    .h(cpu_decoder_4x16_1_out_12), .v(cpu_decoder_4x16_2_out_16), .i(i), .o(cpu_reg_byte_1_o), .s(s), .e(e),
    .RESET(reset), .op(_174));
  CPU_REG_BYTE cpu_reg_byte_28 (
    .h(cpu_decoder_4x16_1_out_13), .v(cpu_decoder_4x16_2_out_16), .i(i), .o(cpu_reg_byte_1_o), .s(s), .e(e),
    .RESET(reset), .op(_190));
  CPU_REG_BYTE cpu_reg_byte_29 (
    .h(cpu_decoder_4x16_1_out_14), .v(cpu_decoder_4x16_2_out_16), .i(i), .o(cpu_reg_byte_1_o), .s(s), .e(e),
    .RESET(reset), .op(_206));
  CPU_REG_BYTE cpu_reg_byte_30 (
    .h(cpu_decoder_4x16_1_out_15), .v(cpu_decoder_4x16_2_out_16), .i(i), .o(cpu_reg_byte_1_o), .s(s), .e(e),
    .RESET(reset), .op(_222));
  CPU_REG_BYTE cpu_reg_byte_31 (
    .h(cpu_decoder_4x16_1_out_16), .v(cpu_decoder_4x16_2_out_16), .i(i), .o(cpu_reg_byte_1_o), .s(s), .e(e),
    .RESET(reset), .op(_238));
  CPU_REG_BYTE cpu_reg_byte_32 (
    .h(cpu_decoder_4x16_1_m), .v(cpu_decoder_4x16_2_out_16), .i(i), .o(cpu_reg_byte_1_o), .s(s), .e(e),
    .RESET(reset), .op(_254));
  CPU_REG_BYTE cpu_reg_byte_33 (
    .h(cpu_decoder_4x16_1_l), .v(cpu_decoder_4x16_2_out_15), .i(i), .o(cpu_reg_byte_1_o), .s(s), .e(e),
    .RESET(reset), .op(_13));
  CPU_REG_BYTE cpu_reg_byte_34 (
    .h(cpu_decoder_4x16_1_out_3), .v(cpu_decoder_4x16_2_out_15), .i(i), .o(cpu_reg_byte_1_o), .s(s), .e(e),
    .RESET(reset), .op(_29));
  CPU_REG_BYTE cpu_reg_byte_35 (
    .h(cpu_decoder_4x16_1_out_4), .v(cpu_decoder_4x16_2_out_15), .i(i), .o(cpu_reg_byte_1_o), .s(s), .e(e),
    .RESET(reset), .op(_45));
  CPU_REG_BYTE cpu_reg_byte_36 (
    .h(cpu_decoder_4x16_1_out_5), .v(cpu_decoder_4x16_2_out_15), .i(i), .o(cpu_reg_byte_1_o), .s(s), .e(e),
    .RESET(reset), .op(_61));
  CPU_REG_BYTE cpu_reg_byte_37 (
    .h(cpu_decoder_4x16_1_out_6), .v(cpu_decoder_4x16_2_out_15), .i(i), .o(cpu_reg_byte_1_o), .s(s), .e(e),
    .RESET(reset), .op(_77));
  CPU_REG_BYTE cpu_reg_byte_38 (
    .h(cpu_decoder_4x16_1_out_7), .v(cpu_decoder_4x16_2_out_15), .i(i), .o(cpu_reg_byte_1_o), .s(s), .e(e),
    .RESET(reset), .op(_93));
  CPU_REG_BYTE cpu_reg_byte_39 (
    .h(cpu_decoder_4x16_1_out_8), .v(cpu_decoder_4x16_2_out_15), .i(i), .o(cpu_reg_byte_1_o), .s(s), .e(e),
    .RESET(reset), .op(_109));
  CPU_REG_BYTE cpu_reg_byte_40 (
    .h(cpu_decoder_4x16_1_out_9), .v(cpu_decoder_4x16_2_out_15), .i(i), .o(cpu_reg_byte_1_o), .s(s), .e(e),
    .RESET(reset), .op(_125));
  CPU_REG_BYTE cpu_reg_byte_41 (
    .h(cpu_decoder_4x16_1_out_10), .v(cpu_decoder_4x16_2_out_15), .i(i), .o(cpu_reg_byte_1_o), .s(s), .e(e),
    .RESET(reset), .op(_141));
  CPU_REG_BYTE cpu_reg_byte_42 (
    .h(cpu_decoder_4x16_1_out_11), .v(cpu_decoder_4x16_2_out_15), .i(i), .o(cpu_reg_byte_1_o), .s(s), .e(e),
    .RESET(reset), .op(_157));
  CPU_REG_BYTE cpu_reg_byte_43 (
    .h(cpu_decoder_4x16_1_out_12), .v(cpu_decoder_4x16_2_out_15), .i(i), .o(cpu_reg_byte_1_o), .s(s), .e(e),
    .RESET(reset), .op(_173));
  CPU_REG_BYTE cpu_reg_byte_44 (
    .h(cpu_decoder_4x16_1_out_13), .v(cpu_decoder_4x16_2_out_15), .i(i), .o(cpu_reg_byte_1_o), .s(s), .e(e),
    .RESET(reset), .op(_189));
  CPU_REG_BYTE cpu_reg_byte_45 (
    .h(cpu_decoder_4x16_1_out_14), .v(cpu_decoder_4x16_2_out_15), .i(i), .o(cpu_reg_byte_1_o), .s(s), .e(e),
    .RESET(reset), .op(_205));
  CPU_REG_BYTE cpu_reg_byte_46 (
    .h(cpu_decoder_4x16_1_out_15), .v(cpu_decoder_4x16_2_out_15), .i(i), .o(cpu_reg_byte_1_o), .s(s), .e(e),
    .RESET(reset), .op(_221));
  CPU_REG_BYTE cpu_reg_byte_47 (
    .h(cpu_decoder_4x16_1_out_16), .v(cpu_decoder_4x16_2_out_15), .i(i), .o(cpu_reg_byte_1_o), .s(s), .e(e),
    .RESET(reset), .op(_237));
  CPU_REG_BYTE cpu_reg_byte_48 (
    .h(cpu_decoder_4x16_1_m), .v(cpu_decoder_4x16_2_out_15), .i(i), .o(cpu_reg_byte_1_o), .s(s), .e(e),
    .RESET(reset), .op(_253));
  CPU_REG_BYTE cpu_reg_byte_49 (
    .h(cpu_decoder_4x16_1_l), .v(cpu_decoder_4x16_2_out_14), .i(i), .o(cpu_reg_byte_1_o), .s(s), .e(e),
    .RESET(reset), .op(_12));
  CPU_REG_BYTE cpu_reg_byte_50 (
    .h(cpu_decoder_4x16_1_out_3), .v(cpu_decoder_4x16_2_out_14), .i(i), .o(cpu_reg_byte_1_o), .s(s), .e(e),
    .RESET(reset), .op(_28));
  CPU_REG_BYTE cpu_reg_byte_51 (
    .h(cpu_decoder_4x16_1_out_4), .v(cpu_decoder_4x16_2_out_14), .i(i), .o(cpu_reg_byte_1_o), .s(s), .e(e),
    .RESET(reset), .op(_44));
  CPU_REG_BYTE cpu_reg_byte_52 (
    .h(cpu_decoder_4x16_1_out_5), .v(cpu_decoder_4x16_2_out_14), .i(i), .o(cpu_reg_byte_1_o), .s(s), .e(e),
    .RESET(reset), .op(_60));
  CPU_REG_BYTE cpu_reg_byte_53 (
    .h(cpu_decoder_4x16_1_out_6), .v(cpu_decoder_4x16_2_out_14), .i(i), .o(cpu_reg_byte_1_o), .s(s), .e(e),
    .RESET(reset), .op(_76));
  CPU_REG_BYTE cpu_reg_byte_54 (
    .h(cpu_decoder_4x16_1_out_7), .v(cpu_decoder_4x16_2_out_14), .i(i), .o(cpu_reg_byte_1_o), .s(s), .e(e),
    .RESET(reset), .op(_92));
  CPU_REG_BYTE cpu_reg_byte_55 (
    .h(cpu_decoder_4x16_1_out_8), .v(cpu_decoder_4x16_2_out_14), .i(i), .o(cpu_reg_byte_1_o), .s(s), .e(e),
    .RESET(reset), .op(_108));
  CPU_REG_BYTE cpu_reg_byte_56 (
    .h(cpu_decoder_4x16_1_out_9), .v(cpu_decoder_4x16_2_out_14), .i(i), .o(cpu_reg_byte_1_o), .s(s), .e(e),
    .RESET(reset), .op(_124));
  CPU_REG_BYTE cpu_reg_byte_57 (
    .h(cpu_decoder_4x16_1_out_10), .v(cpu_decoder_4x16_2_out_14), .i(i), .o(cpu_reg_byte_1_o), .s(s), .e(e),
    .RESET(reset), .op(_140));
  CPU_REG_BYTE cpu_reg_byte_58 (
    .h(cpu_decoder_4x16_1_out_11), .v(cpu_decoder_4x16_2_out_14), .i(i), .o(cpu_reg_byte_1_o), .s(s), .e(e),
    .RESET(reset), .op(_156));
  CPU_REG_BYTE cpu_reg_byte_59 (
    .h(cpu_decoder_4x16_1_out_12), .v(cpu_decoder_4x16_2_out_14), .i(i), .o(cpu_reg_byte_1_o), .s(s), .e(e),
    .RESET(reset), .op(_172));
  CPU_REG_BYTE cpu_reg_byte_60 (
    .h(cpu_decoder_4x16_1_out_13), .v(cpu_decoder_4x16_2_out_14), .i(i), .o(cpu_reg_byte_1_o), .s(s), .e(e),
    .RESET(reset), .op(_188));
  CPU_REG_BYTE cpu_reg_byte_61 (
    .h(cpu_decoder_4x16_1_out_14), .v(cpu_decoder_4x16_2_out_14), .i(i), .o(cpu_reg_byte_1_o), .s(s), .e(e),
    .RESET(reset), .op(_204));
  CPU_REG_BYTE cpu_reg_byte_62 (
    .h(cpu_decoder_4x16_1_out_15), .v(cpu_decoder_4x16_2_out_14), .i(i), .o(cpu_reg_byte_1_o), .s(s), .e(e),
    .RESET(reset), .op(_220));
  CPU_REG_BYTE cpu_reg_byte_63 (
    .h(cpu_decoder_4x16_1_out_16), .v(cpu_decoder_4x16_2_out_14), .i(i), .o(cpu_reg_byte_1_o), .s(s), .e(e),
    .RESET(reset), .op(_236));
  CPU_REG_BYTE cpu_reg_byte_64 (
    .h(cpu_decoder_4x16_1_m), .v(cpu_decoder_4x16_2_out_14), .i(i), .o(cpu_reg_byte_1_o), .s(s), .e(e),
    .RESET(reset), .op(_252));
  CPU_REG_BYTE cpu_reg_byte_65 (
    .h(cpu_decoder_4x16_1_l), .v(cpu_decoder_4x16_2_out_13), .i(i), .o(cpu_reg_byte_1_o), .s(s), .e(e),
    .RESET(reset), .op(_11));
  CPU_REG_BYTE cpu_reg_byte_66 (
    .h(cpu_decoder_4x16_1_out_3), .v(cpu_decoder_4x16_2_out_13), .i(i), .o(cpu_reg_byte_1_o), .s(s), .e(e),
    .RESET(reset), .op(_27));
  CPU_REG_BYTE cpu_reg_byte_67 (
    .h(cpu_decoder_4x16_1_out_4), .v(cpu_decoder_4x16_2_out_13), .i(i), .o(cpu_reg_byte_1_o), .s(s), .e(e),
    .RESET(reset), .op(_43));
  CPU_REG_BYTE cpu_reg_byte_68 (
    .h(cpu_decoder_4x16_1_out_5), .v(cpu_decoder_4x16_2_out_13), .i(i), .o(cpu_reg_byte_1_o), .s(s), .e(e),
    .RESET(reset), .op(_59));
  CPU_REG_BYTE cpu_reg_byte_69 (
    .h(cpu_decoder_4x16_1_out_6), .v(cpu_decoder_4x16_2_out_13), .i(i), .o(cpu_reg_byte_1_o), .s(s), .e(e),
    .RESET(reset), .op(_75));
  CPU_REG_BYTE cpu_reg_byte_70 (
    .h(cpu_decoder_4x16_1_out_7), .v(cpu_decoder_4x16_2_out_13), .i(i), .o(cpu_reg_byte_1_o), .s(s), .e(e),
    .RESET(reset), .op(_91));
  CPU_REG_BYTE cpu_reg_byte_71 (
    .h(cpu_decoder_4x16_1_out_8), .v(cpu_decoder_4x16_2_out_13), .i(i), .o(cpu_reg_byte_1_o), .s(s), .e(e),
    .RESET(reset), .op(_107));
  CPU_REG_BYTE cpu_reg_byte_72 (
    .h(cpu_decoder_4x16_1_out_9), .v(cpu_decoder_4x16_2_out_13), .i(i), .o(cpu_reg_byte_1_o), .s(s), .e(e),
    .RESET(reset), .op(_123));
  CPU_REG_BYTE cpu_reg_byte_73 (
    .h(cpu_decoder_4x16_1_out_10), .v(cpu_decoder_4x16_2_out_13), .i(i), .o(cpu_reg_byte_1_o), .s(s), .e(e),
    .RESET(reset), .op(_139));
  CPU_REG_BYTE cpu_reg_byte_74 (
    .h(cpu_decoder_4x16_1_out_11), .v(cpu_decoder_4x16_2_out_13), .i(i), .o(cpu_reg_byte_1_o), .s(s), .e(e),
    .RESET(reset), .op(_155));
  CPU_REG_BYTE cpu_reg_byte_75 (
    .h(cpu_decoder_4x16_1_out_12), .v(cpu_decoder_4x16_2_out_13), .i(i), .o(cpu_reg_byte_1_o), .s(s), .e(e),
    .RESET(reset), .op(_171));
  CPU_REG_BYTE cpu_reg_byte_76 (
    .h(cpu_decoder_4x16_1_out_13), .v(cpu_decoder_4x16_2_out_13), .i(i), .o(cpu_reg_byte_1_o), .s(s), .e(e),
    .RESET(reset), .op(_187));
  CPU_REG_BYTE cpu_reg_byte_77 (
    .h(cpu_decoder_4x16_1_out_14), .v(cpu_decoder_4x16_2_out_13), .i(i), .o(cpu_reg_byte_1_o), .s(s), .e(e),
    .RESET(reset), .op(_203));
  CPU_REG_BYTE cpu_reg_byte_78 (
    .h(cpu_decoder_4x16_1_out_15), .v(cpu_decoder_4x16_2_out_13), .i(i), .o(cpu_reg_byte_1_o), .s(s), .e(e),
    .RESET(reset), .op(_219));
  CPU_REG_BYTE cpu_reg_byte_79 (
    .h(cpu_decoder_4x16_1_out_16), .v(cpu_decoder_4x16_2_out_13), .i(i), .o(cpu_reg_byte_1_o), .s(s), .e(e),
    .RESET(reset), .op(_235));
  CPU_REG_BYTE cpu_reg_byte_80 (
    .h(cpu_decoder_4x16_1_m), .v(cpu_decoder_4x16_2_out_13), .i(i), .o(cpu_reg_byte_1_o), .s(s), .e(e),
    .RESET(reset), .op(_251));
  CPU_REG_BYTE cpu_reg_byte_81 (
    .h(cpu_decoder_4x16_1_l), .v(cpu_decoder_4x16_2_out_12), .i(i), .o(cpu_reg_byte_1_o), .s(s), .e(e),
    .RESET(reset), .op(_10));
  CPU_REG_BYTE cpu_reg_byte_82 (
    .h(cpu_decoder_4x16_1_out_3), .v(cpu_decoder_4x16_2_out_12), .i(i), .o(cpu_reg_byte_1_o), .s(s), .e(e),
    .RESET(reset), .op(_26));
  CPU_REG_BYTE cpu_reg_byte_83 (
    .h(cpu_decoder_4x16_1_out_4), .v(cpu_decoder_4x16_2_out_12), .i(i), .o(cpu_reg_byte_1_o), .s(s), .e(e),
    .RESET(reset), .op(_42));
  CPU_REG_BYTE cpu_reg_byte_84 (
    .h(cpu_decoder_4x16_1_out_5), .v(cpu_decoder_4x16_2_out_12), .i(i), .o(cpu_reg_byte_1_o), .s(s), .e(e),
    .RESET(reset), .op(_58));
  CPU_REG_BYTE cpu_reg_byte_85 (
    .h(cpu_decoder_4x16_1_out_6), .v(cpu_decoder_4x16_2_out_12), .i(i), .o(cpu_reg_byte_1_o), .s(s), .e(e),
    .RESET(reset), .op(_74));
  CPU_REG_BYTE cpu_reg_byte_86 (
    .h(cpu_decoder_4x16_1_out_7), .v(cpu_decoder_4x16_2_out_12), .i(i), .o(cpu_reg_byte_1_o), .s(s), .e(e),
    .RESET(reset), .op(_90));
  CPU_REG_BYTE cpu_reg_byte_87 (
    .h(cpu_decoder_4x16_1_out_8), .v(cpu_decoder_4x16_2_out_12), .i(i), .o(cpu_reg_byte_1_o), .s(s), .e(e),
    .RESET(reset), .op(_106));
  CPU_REG_BYTE cpu_reg_byte_88 (
    .h(cpu_decoder_4x16_1_out_9), .v(cpu_decoder_4x16_2_out_12), .i(i), .o(cpu_reg_byte_1_o), .s(s), .e(e),
    .RESET(reset), .op(_122));
  CPU_REG_BYTE cpu_reg_byte_89 (
    .h(cpu_decoder_4x16_1_out_10), .v(cpu_decoder_4x16_2_out_12), .i(i), .o(cpu_reg_byte_1_o), .s(s), .e(e),
    .RESET(reset), .op(_138));
  CPU_REG_BYTE cpu_reg_byte_90 (
    .h(cpu_decoder_4x16_1_out_11), .v(cpu_decoder_4x16_2_out_12), .i(i), .o(cpu_reg_byte_1_o), .s(s), .e(e),
    .RESET(reset), .op(_154));
  CPU_REG_BYTE cpu_reg_byte_91 (
    .h(cpu_decoder_4x16_1_out_12), .v(cpu_decoder_4x16_2_out_12), .i(i), .o(cpu_reg_byte_1_o), .s(s), .e(e),
    .RESET(reset), .op(_170));
  CPU_REG_BYTE cpu_reg_byte_92 (
    .h(cpu_decoder_4x16_1_out_13), .v(cpu_decoder_4x16_2_out_12), .i(i), .o(cpu_reg_byte_1_o), .s(s), .e(e),
    .RESET(reset), .op(_186));
  CPU_REG_BYTE cpu_reg_byte_93 (
    .h(cpu_decoder_4x16_1_out_14), .v(cpu_decoder_4x16_2_out_12), .i(i), .o(cpu_reg_byte_1_o), .s(s), .e(e),
    .RESET(reset), .op(_202));
  CPU_REG_BYTE cpu_reg_byte_94 (
    .h(cpu_decoder_4x16_1_out_15), .v(cpu_decoder_4x16_2_out_12), .i(i), .o(cpu_reg_byte_1_o), .s(s), .e(e),
    .RESET(reset), .op(_218));
  CPU_REG_BYTE cpu_reg_byte_95 (
    .h(cpu_decoder_4x16_1_out_16), .v(cpu_decoder_4x16_2_out_12), .i(i), .o(cpu_reg_byte_1_o), .s(s), .e(e),
    .RESET(reset), .op(_234));
  CPU_REG_BYTE cpu_reg_byte_96 (
    .h(cpu_decoder_4x16_1_m), .v(cpu_decoder_4x16_2_out_12), .i(i), .o(cpu_reg_byte_1_o), .s(s), .e(e),
    .RESET(reset), .op(_250));
  CPU_REG_BYTE cpu_reg_byte_97 (
    .h(cpu_decoder_4x16_1_l), .v(cpu_decoder_4x16_2_out_11), .i(i), .o(cpu_reg_byte_1_o), .s(s), .e(e),
    .RESET(reset), .op(_9));
  CPU_REG_BYTE cpu_reg_byte_98 (
    .h(cpu_decoder_4x16_1_out_3), .v(cpu_decoder_4x16_2_out_11), .i(i), .o(cpu_reg_byte_1_o), .s(s), .e(e),
    .RESET(reset), .op(_25));
  CPU_REG_BYTE cpu_reg_byte_99 (
    .h(cpu_decoder_4x16_1_out_4), .v(cpu_decoder_4x16_2_out_11), .i(i), .o(cpu_reg_byte_1_o), .s(s), .e(e),
    .RESET(reset), .op(_41));
  CPU_REG_BYTE cpu_reg_byte_100 (
    .h(cpu_decoder_4x16_1_out_5), .v(cpu_decoder_4x16_2_out_11), .i(i), .o(cpu_reg_byte_1_o), .s(s), .e(e),
    .RESET(reset), .op(_57));
  CPU_REG_BYTE cpu_reg_byte_101 (
    .h(cpu_decoder_4x16_1_out_6), .v(cpu_decoder_4x16_2_out_11), .i(i), .o(cpu_reg_byte_1_o), .s(s), .e(e),
    .RESET(reset), .op(_73));
  CPU_REG_BYTE cpu_reg_byte_102 (
    .h(cpu_decoder_4x16_1_out_7), .v(cpu_decoder_4x16_2_out_11), .i(i), .o(cpu_reg_byte_1_o), .s(s), .e(e),
    .RESET(reset), .op(_89));
  CPU_REG_BYTE cpu_reg_byte_103 (
    .h(cpu_decoder_4x16_1_out_8), .v(cpu_decoder_4x16_2_out_11), .i(i), .o(cpu_reg_byte_1_o), .s(s), .e(e),
    .RESET(reset), .op(_105));
  CPU_REG_BYTE cpu_reg_byte_104 (
    .h(cpu_decoder_4x16_1_out_9), .v(cpu_decoder_4x16_2_out_11), .i(i), .o(cpu_reg_byte_1_o), .s(s), .e(e),
    .RESET(reset), .op(_121));
  CPU_REG_BYTE cpu_reg_byte_105 (
    .h(cpu_decoder_4x16_1_out_10), .v(cpu_decoder_4x16_2_out_11), .i(i), .o(cpu_reg_byte_1_o), .s(s), .e(e),
    .RESET(reset), .op(_137));
  CPU_REG_BYTE cpu_reg_byte_106 (
    .h(cpu_decoder_4x16_1_out_11), .v(cpu_decoder_4x16_2_out_11), .i(i), .o(cpu_reg_byte_1_o), .s(s), .e(e),
    .RESET(reset), .op(_153));
  CPU_REG_BYTE cpu_reg_byte_107 (
    .h(cpu_decoder_4x16_1_out_12), .v(cpu_decoder_4x16_2_out_11), .i(i), .o(cpu_reg_byte_1_o), .s(s), .e(e),
    .RESET(reset), .op(_169));
  CPU_REG_BYTE cpu_reg_byte_108 (
    .h(cpu_decoder_4x16_1_out_13), .v(cpu_decoder_4x16_2_out_11), .i(i), .o(cpu_reg_byte_1_o), .s(s), .e(e),
    .RESET(reset), .op(_185));
  CPU_REG_BYTE cpu_reg_byte_109 (
    .h(cpu_decoder_4x16_1_out_14), .v(cpu_decoder_4x16_2_out_11), .i(i), .o(cpu_reg_byte_1_o), .s(s), .e(e),
    .RESET(reset), .op(_201));
  CPU_REG_BYTE cpu_reg_byte_110 (
    .h(cpu_decoder_4x16_1_out_15), .v(cpu_decoder_4x16_2_out_11), .i(i), .o(cpu_reg_byte_1_o), .s(s), .e(e),
    .RESET(reset), .op(_217));
  CPU_REG_BYTE cpu_reg_byte_111 (
    .h(cpu_decoder_4x16_1_out_16), .v(cpu_decoder_4x16_2_out_11), .i(i), .o(cpu_reg_byte_1_o), .s(s), .e(e),
    .RESET(reset), .op(_233));
  CPU_REG_BYTE cpu_reg_byte_112 (
    .h(cpu_decoder_4x16_1_m), .v(cpu_decoder_4x16_2_out_11), .i(i), .o(cpu_reg_byte_1_o), .s(s), .e(e),
    .RESET(reset), .op(_249));
  CPU_REG_BYTE cpu_reg_byte_113 (
    .h(cpu_decoder_4x16_1_l), .v(cpu_decoder_4x16_2_out_10), .i(i), .o(cpu_reg_byte_1_o), .s(s), .e(e),
    .RESET(reset), .op(_8));
  CPU_REG_BYTE cpu_reg_byte_114 (
    .h(cpu_decoder_4x16_1_out_3), .v(cpu_decoder_4x16_2_out_10), .i(i), .o(cpu_reg_byte_1_o), .s(s), .e(e),
    .RESET(reset), .op(_24));
  CPU_REG_BYTE cpu_reg_byte_115 (
    .h(cpu_decoder_4x16_1_out_4), .v(cpu_decoder_4x16_2_out_10), .i(i), .o(cpu_reg_byte_1_o), .s(s), .e(e),
    .RESET(reset), .op(_40));
  CPU_REG_BYTE cpu_reg_byte_116 (
    .h(cpu_decoder_4x16_1_out_5), .v(cpu_decoder_4x16_2_out_10), .i(i), .o(cpu_reg_byte_1_o), .s(s), .e(e),
    .RESET(reset), .op(_56));
  CPU_REG_BYTE cpu_reg_byte_117 (
    .h(cpu_decoder_4x16_1_out_6), .v(cpu_decoder_4x16_2_out_10), .i(i), .o(cpu_reg_byte_1_o), .s(s), .e(e),
    .RESET(reset), .op(_72));
  CPU_REG_BYTE cpu_reg_byte_118 (
    .h(cpu_decoder_4x16_1_out_7), .v(cpu_decoder_4x16_2_out_10), .i(i), .o(cpu_reg_byte_1_o), .s(s), .e(e),
    .RESET(reset), .op(_88));
  CPU_REG_BYTE cpu_reg_byte_119 (
    .h(cpu_decoder_4x16_1_out_8), .v(cpu_decoder_4x16_2_out_10), .i(i), .o(cpu_reg_byte_1_o), .s(s), .e(e),
    .RESET(reset), .op(_104));
  CPU_REG_BYTE cpu_reg_byte_120 (
    .h(cpu_decoder_4x16_1_out_9), .v(cpu_decoder_4x16_2_out_10), .i(i), .o(cpu_reg_byte_1_o), .s(s), .e(e),
    .RESET(reset), .op(_120));
  CPU_REG_BYTE cpu_reg_byte_121 (
    .h(cpu_decoder_4x16_1_out_10), .v(cpu_decoder_4x16_2_out_10), .i(i), .o(cpu_reg_byte_1_o), .s(s), .e(e),
    .RESET(reset), .op(_136));
  CPU_REG_BYTE cpu_reg_byte_122 (
    .h(cpu_decoder_4x16_1_out_11), .v(cpu_decoder_4x16_2_out_10), .i(i), .o(cpu_reg_byte_1_o), .s(s), .e(e),
    .RESET(reset), .op(_152));
  CPU_REG_BYTE cpu_reg_byte_123 (
    .h(cpu_decoder_4x16_1_out_12), .v(cpu_decoder_4x16_2_out_10), .i(i), .o(cpu_reg_byte_1_o), .s(s), .e(e),
    .RESET(reset), .op(_168));
  CPU_REG_BYTE cpu_reg_byte_124 (
    .h(cpu_decoder_4x16_1_out_13), .v(cpu_decoder_4x16_2_out_10), .i(i), .o(cpu_reg_byte_1_o), .s(s), .e(e),
    .RESET(reset), .op(_184));
  CPU_REG_BYTE cpu_reg_byte_125 (
    .h(cpu_decoder_4x16_1_out_14), .v(cpu_decoder_4x16_2_out_10), .i(i), .o(cpu_reg_byte_1_o), .s(s), .e(e),
    .RESET(reset), .op(_200));
  CPU_REG_BYTE cpu_reg_byte_126 (
    .h(cpu_decoder_4x16_1_out_15), .v(cpu_decoder_4x16_2_out_10), .i(i), .o(cpu_reg_byte_1_o), .s(s), .e(e),
    .RESET(reset), .op(_216));
  CPU_REG_BYTE cpu_reg_byte_127 (
    .h(cpu_decoder_4x16_1_out_16), .v(cpu_decoder_4x16_2_out_10), .i(i), .o(cpu_reg_byte_1_o), .s(s), .e(e),
    .RESET(reset), .op(_232));
  CPU_REG_BYTE cpu_reg_byte_128 (
    .h(cpu_decoder_4x16_1_m), .v(cpu_decoder_4x16_2_out_10), .i(i), .o(cpu_reg_byte_1_o), .s(s), .e(e),
    .RESET(reset), .op(_248));
  CPU_DECODER_4x16 cpu_decoder_4x16_2 (
    .in_1(cpu_mem_8_1_out_3[3:0]), .L(cpu_decoder_4x16_2_l), .out_3(cpu_decoder_4x16_2_out_3),
    .out_4(cpu_decoder_4x16_2_out_4), .out_5(cpu_decoder_4x16_2_out_5), .out_6(cpu_decoder_4x16_2_out_6),
    .out_7(cpu_decoder_4x16_2_out_7), .out_8(cpu_decoder_4x16_2_out_8), .out_9(cpu_decoder_4x16_2_out_9),
    .out_10(cpu_decoder_4x16_2_out_10), .out_11(cpu_decoder_4x16_2_out_11),
    .out_12(cpu_decoder_4x16_2_out_12), .out_13(cpu_decoder_4x16_2_out_13),
    .out_14(cpu_decoder_4x16_2_out_14), .out_15(cpu_decoder_4x16_2_out_15),
    .out_16(cpu_decoder_4x16_2_out_16), .M(cpu_decoder_4x16_2_m));
  CPU_REG_BYTE cpu_reg_byte_129 (
    .h(cpu_decoder_4x16_1_l), .v(cpu_decoder_4x16_2_out_9), .i(i), .o(cpu_reg_byte_1_o), .s(s), .e(e),
    .RESET(reset), .op(_7));
  CPU_REG_BYTE cpu_reg_byte_130 (
    .h(cpu_decoder_4x16_1_out_3), .v(cpu_decoder_4x16_2_out_9), .i(i), .o(cpu_reg_byte_1_o), .s(s), .e(e),
    .RESET(reset), .op(_23));
  CPU_REG_BYTE cpu_reg_byte_131 (
    .h(cpu_decoder_4x16_1_out_4), .v(cpu_decoder_4x16_2_out_9), .i(i), .o(cpu_reg_byte_1_o), .s(s), .e(e),
    .RESET(reset), .op(_39));
  CPU_REG_BYTE cpu_reg_byte_132 (
    .h(cpu_decoder_4x16_1_out_5), .v(cpu_decoder_4x16_2_out_9), .i(i), .o(cpu_reg_byte_1_o), .s(s), .e(e),
    .RESET(reset), .op(_55));
  CPU_REG_BYTE cpu_reg_byte_133 (
    .h(cpu_decoder_4x16_1_out_6), .v(cpu_decoder_4x16_2_out_9), .i(i), .o(cpu_reg_byte_1_o), .s(s), .e(e),
    .RESET(reset), .op(_71));
  CPU_REG_BYTE cpu_reg_byte_134 (
    .h(cpu_decoder_4x16_1_out_7), .v(cpu_decoder_4x16_2_out_9), .i(i), .o(cpu_reg_byte_1_o), .s(s), .e(e),
    .RESET(reset), .op(_87));
  CPU_REG_BYTE cpu_reg_byte_135 (
    .h(cpu_decoder_4x16_1_out_8), .v(cpu_decoder_4x16_2_out_9), .i(i), .o(cpu_reg_byte_1_o), .s(s), .e(e),
    .RESET(reset), .op(_103));
  CPU_REG_BYTE cpu_reg_byte_136 (
    .h(cpu_decoder_4x16_1_out_9), .v(cpu_decoder_4x16_2_out_9), .i(i), .o(cpu_reg_byte_1_o), .s(s), .e(e),
    .RESET(reset), .op(_119));
  CPU_REG_BYTE cpu_reg_byte_137 (
    .h(cpu_decoder_4x16_1_out_10), .v(cpu_decoder_4x16_2_out_9), .i(i), .o(cpu_reg_byte_1_o), .s(s), .e(e),
    .RESET(reset), .op(_135));
  CPU_REG_BYTE cpu_reg_byte_138 (
    .h(cpu_decoder_4x16_1_out_11), .v(cpu_decoder_4x16_2_out_9), .i(i), .o(cpu_reg_byte_1_o), .s(s), .e(e),
    .RESET(reset), .op(_151));
  CPU_REG_BYTE cpu_reg_byte_139 (
    .h(cpu_decoder_4x16_1_out_12), .v(cpu_decoder_4x16_2_out_9), .i(i), .o(cpu_reg_byte_1_o), .s(s), .e(e),
    .RESET(reset), .op(_167));
  CPU_REG_BYTE cpu_reg_byte_140 (
    .h(cpu_decoder_4x16_1_out_13), .v(cpu_decoder_4x16_2_out_9), .i(i), .o(cpu_reg_byte_1_o), .s(s), .e(e),
    .RESET(reset), .op(_183));
  CPU_REG_BYTE cpu_reg_byte_141 (
    .h(cpu_decoder_4x16_1_out_14), .v(cpu_decoder_4x16_2_out_9), .i(i), .o(cpu_reg_byte_1_o), .s(s), .e(e),
    .RESET(reset), .op(_199));
  CPU_REG_BYTE cpu_reg_byte_142 (
    .h(cpu_decoder_4x16_1_out_15), .v(cpu_decoder_4x16_2_out_9), .i(i), .o(cpu_reg_byte_1_o), .s(s), .e(e),
    .RESET(reset), .op(_215));
  CPU_REG_BYTE cpu_reg_byte_143 (
    .h(cpu_decoder_4x16_1_out_16), .v(cpu_decoder_4x16_2_out_9), .i(i), .o(cpu_reg_byte_1_o), .s(s), .e(e),
    .RESET(reset), .op(_231));
  CPU_REG_BYTE cpu_reg_byte_144 (
    .h(cpu_decoder_4x16_1_m), .v(cpu_decoder_4x16_2_out_9), .i(i), .o(cpu_reg_byte_1_o), .s(s), .e(e),
    .RESET(reset), .op(_247));
  CPU_REG_BYTE cpu_reg_byte_145 (
    .h(cpu_decoder_4x16_1_l), .v(cpu_decoder_4x16_2_out_8), .i(i), .o(cpu_reg_byte_1_o), .s(s), .e(e),
    .RESET(reset), .op(_6));
  CPU_REG_BYTE cpu_reg_byte_146 (
    .h(cpu_decoder_4x16_1_out_3), .v(cpu_decoder_4x16_2_out_8), .i(i), .o(cpu_reg_byte_1_o), .s(s), .e(e),
    .RESET(reset), .op(_22));
  CPU_REG_BYTE cpu_reg_byte_147 (
    .h(cpu_decoder_4x16_1_out_4), .v(cpu_decoder_4x16_2_out_8), .i(i), .o(cpu_reg_byte_1_o), .s(s), .e(e),
    .RESET(reset), .op(_38));
  CPU_REG_BYTE cpu_reg_byte_148 (
    .h(cpu_decoder_4x16_1_out_5), .v(cpu_decoder_4x16_2_out_8), .i(i), .o(cpu_reg_byte_1_o), .s(s), .e(e),
    .RESET(reset), .op(_54));
  CPU_REG_BYTE cpu_reg_byte_149 (
    .h(cpu_decoder_4x16_1_out_6), .v(cpu_decoder_4x16_2_out_8), .i(i), .o(cpu_reg_byte_1_o), .s(s), .e(e),
    .RESET(reset), .op(_70));
  CPU_REG_BYTE cpu_reg_byte_150 (
    .h(cpu_decoder_4x16_1_out_7), .v(cpu_decoder_4x16_2_out_8), .i(i), .o(cpu_reg_byte_1_o), .s(s), .e(e),
    .RESET(reset), .op(_86));
  CPU_REG_BYTE cpu_reg_byte_151 (
    .h(cpu_decoder_4x16_1_out_8), .v(cpu_decoder_4x16_2_out_8), .i(i), .o(cpu_reg_byte_1_o), .s(s), .e(e),
    .RESET(reset), .op(_102));
  CPU_REG_BYTE cpu_reg_byte_152 (
    .h(cpu_decoder_4x16_1_out_9), .v(cpu_decoder_4x16_2_out_8), .i(i), .o(cpu_reg_byte_1_o), .s(s), .e(e),
    .RESET(reset), .op(_118));
  CPU_REG_BYTE cpu_reg_byte_153 (
    .h(cpu_decoder_4x16_1_out_10), .v(cpu_decoder_4x16_2_out_8), .i(i), .o(cpu_reg_byte_1_o), .s(s), .e(e),
    .RESET(reset), .op(_134));
  CPU_REG_BYTE cpu_reg_byte_154 (
    .h(cpu_decoder_4x16_1_out_11), .v(cpu_decoder_4x16_2_out_8), .i(i), .o(cpu_reg_byte_1_o), .s(s), .e(e),
    .RESET(reset), .op(_150));
  CPU_REG_BYTE cpu_reg_byte_155 (
    .h(cpu_decoder_4x16_1_out_12), .v(cpu_decoder_4x16_2_out_8), .i(i), .o(cpu_reg_byte_1_o), .s(s), .e(e),
    .RESET(reset), .op(_166));
  CPU_REG_BYTE cpu_reg_byte_156 (
    .h(cpu_decoder_4x16_1_out_13), .v(cpu_decoder_4x16_2_out_8), .i(i), .o(cpu_reg_byte_1_o), .s(s), .e(e),
    .RESET(reset), .op(_182));
  CPU_REG_BYTE cpu_reg_byte_157 (
    .h(cpu_decoder_4x16_1_out_14), .v(cpu_decoder_4x16_2_out_8), .i(i), .o(cpu_reg_byte_1_o), .s(s), .e(e),
    .RESET(reset), .op(_198));
  CPU_REG_BYTE cpu_reg_byte_158 (
    .h(cpu_decoder_4x16_1_out_15), .v(cpu_decoder_4x16_2_out_8), .i(i), .o(cpu_reg_byte_1_o), .s(s), .e(e),
    .RESET(reset), .op(_214));
  CPU_REG_BYTE cpu_reg_byte_159 (
    .h(cpu_decoder_4x16_1_out_16), .v(cpu_decoder_4x16_2_out_8), .i(i), .o(cpu_reg_byte_1_o), .s(s), .e(e),
    .RESET(reset), .op(_230));
  CPU_REG_BYTE cpu_reg_byte_160 (
    .h(cpu_decoder_4x16_1_m), .v(cpu_decoder_4x16_2_out_8), .i(i), .o(cpu_reg_byte_1_o), .s(s), .e(e),
    .RESET(reset), .op(_246));
  CPU_REG_BYTE cpu_reg_byte_161 (
    .h(cpu_decoder_4x16_1_l), .v(cpu_decoder_4x16_2_out_7), .i(i), .o(cpu_reg_byte_1_o), .s(s), .e(e),
    .RESET(reset), .op(_5));
  CPU_REG_BYTE cpu_reg_byte_162 (
    .h(cpu_decoder_4x16_1_out_3), .v(cpu_decoder_4x16_2_out_7), .i(i), .o(cpu_reg_byte_1_o), .s(s), .e(e),
    .RESET(reset), .op(_21));
  CPU_REG_BYTE cpu_reg_byte_163 (
    .h(cpu_decoder_4x16_1_out_4), .v(cpu_decoder_4x16_2_out_7), .i(i), .o(cpu_reg_byte_1_o), .s(s), .e(e),
    .RESET(reset), .op(_37));
  CPU_REG_BYTE cpu_reg_byte_164 (
    .h(cpu_decoder_4x16_1_out_5), .v(cpu_decoder_4x16_2_out_7), .i(i), .o(cpu_reg_byte_1_o), .s(s), .e(e),
    .RESET(reset), .op(_53));
  CPU_REG_BYTE cpu_reg_byte_165 (
    .h(cpu_decoder_4x16_1_out_6), .v(cpu_decoder_4x16_2_out_7), .i(i), .o(cpu_reg_byte_1_o), .s(s), .e(e),
    .RESET(reset), .op(_69));
  CPU_REG_BYTE cpu_reg_byte_166 (
    .h(cpu_decoder_4x16_1_out_7), .v(cpu_decoder_4x16_2_out_7), .i(i), .o(cpu_reg_byte_1_o), .s(s), .e(e),
    .RESET(reset), .op(_85));
  CPU_REG_BYTE cpu_reg_byte_167 (
    .h(cpu_decoder_4x16_1_out_8), .v(cpu_decoder_4x16_2_out_7), .i(i), .o(cpu_reg_byte_1_o), .s(s), .e(e),
    .RESET(reset), .op(_101));
  CPU_REG_BYTE cpu_reg_byte_168 (
    .h(cpu_decoder_4x16_1_out_9), .v(cpu_decoder_4x16_2_out_7), .i(i), .o(cpu_reg_byte_1_o), .s(s), .e(e),
    .RESET(reset), .op(_117));
  CPU_REG_BYTE cpu_reg_byte_169 (
    .h(cpu_decoder_4x16_1_out_10), .v(cpu_decoder_4x16_2_out_7), .i(i), .o(cpu_reg_byte_1_o), .s(s), .e(e),
    .RESET(reset), .op(_133));
  CPU_REG_BYTE cpu_reg_byte_170 (
    .h(cpu_decoder_4x16_1_out_11), .v(cpu_decoder_4x16_2_out_7), .i(i), .o(cpu_reg_byte_1_o), .s(s), .e(e),
    .RESET(reset), .op(_149));
  CPU_REG_BYTE cpu_reg_byte_171 (
    .h(cpu_decoder_4x16_1_out_12), .v(cpu_decoder_4x16_2_out_7), .i(i), .o(cpu_reg_byte_1_o), .s(s), .e(e),
    .RESET(reset), .op(_165));
  CPU_REG_BYTE cpu_reg_byte_172 (
    .h(cpu_decoder_4x16_1_out_13), .v(cpu_decoder_4x16_2_out_7), .i(i), .o(cpu_reg_byte_1_o), .s(s), .e(e),
    .RESET(reset), .op(_181));
  CPU_REG_BYTE cpu_reg_byte_173 (
    .h(cpu_decoder_4x16_1_out_14), .v(cpu_decoder_4x16_2_out_7), .i(i), .o(cpu_reg_byte_1_o), .s(s), .e(e),
    .RESET(reset), .op(_197));
  CPU_REG_BYTE cpu_reg_byte_174 (
    .h(cpu_decoder_4x16_1_out_15), .v(cpu_decoder_4x16_2_out_7), .i(i), .o(cpu_reg_byte_1_o), .s(s), .e(e),
    .RESET(reset), .op(_213));
  CPU_REG_BYTE cpu_reg_byte_175 (
    .h(cpu_decoder_4x16_1_out_16), .v(cpu_decoder_4x16_2_out_7), .i(i), .o(cpu_reg_byte_1_o), .s(s), .e(e),
    .RESET(reset), .op(_229));
  CPU_REG_BYTE cpu_reg_byte_176 (
    .h(cpu_decoder_4x16_1_m), .v(cpu_decoder_4x16_2_out_7), .i(i), .o(cpu_reg_byte_1_o), .s(s), .e(e),
    .RESET(reset), .op(_245));
  CPU_REG_BYTE cpu_reg_byte_177 (
    .h(cpu_decoder_4x16_1_l), .v(cpu_decoder_4x16_2_out_6), .i(i), .o(cpu_reg_byte_1_o), .s(s), .e(e),
    .RESET(reset), .op(_4));
  CPU_REG_BYTE cpu_reg_byte_178 (
    .h(cpu_decoder_4x16_1_out_3), .v(cpu_decoder_4x16_2_out_6), .i(i), .o(cpu_reg_byte_1_o), .s(s), .e(e),
    .RESET(reset), .op(_20));
  CPU_REG_BYTE cpu_reg_byte_179 (
    .h(cpu_decoder_4x16_1_out_4), .v(cpu_decoder_4x16_2_out_6), .i(i), .o(cpu_reg_byte_1_o), .s(s), .e(e),
    .RESET(reset), .op(_36));
  CPU_REG_BYTE cpu_reg_byte_180 (
    .h(cpu_decoder_4x16_1_out_5), .v(cpu_decoder_4x16_2_out_6), .i(i), .o(cpu_reg_byte_1_o), .s(s), .e(e),
    .RESET(reset), .op(_52));
  CPU_REG_BYTE cpu_reg_byte_181 (
    .h(cpu_decoder_4x16_1_out_6), .v(cpu_decoder_4x16_2_out_6), .i(i), .o(cpu_reg_byte_1_o), .s(s), .e(e),
    .RESET(reset), .op(_68));
  CPU_REG_BYTE cpu_reg_byte_182 (
    .h(cpu_decoder_4x16_1_out_7), .v(cpu_decoder_4x16_2_out_6), .i(i), .o(cpu_reg_byte_1_o), .s(s), .e(e),
    .RESET(reset), .op(_84));
  CPU_REG_BYTE cpu_reg_byte_183 (
    .h(cpu_decoder_4x16_1_out_8), .v(cpu_decoder_4x16_2_out_6), .i(i), .o(cpu_reg_byte_1_o), .s(s), .e(e),
    .RESET(reset), .op(_100));
  CPU_REG_BYTE cpu_reg_byte_184 (
    .h(cpu_decoder_4x16_1_out_9), .v(cpu_decoder_4x16_2_out_6), .i(i), .o(cpu_reg_byte_1_o), .s(s), .e(e),
    .RESET(reset), .op(_116));
  CPU_REG_BYTE cpu_reg_byte_185 (
    .h(cpu_decoder_4x16_1_out_10), .v(cpu_decoder_4x16_2_out_6), .i(i), .o(cpu_reg_byte_1_o), .s(s), .e(e),
    .RESET(reset), .op(_132));
  CPU_REG_BYTE cpu_reg_byte_186 (
    .h(cpu_decoder_4x16_1_out_11), .v(cpu_decoder_4x16_2_out_6), .i(i), .o(cpu_reg_byte_1_o), .s(s), .e(e),
    .RESET(reset), .op(_148));
  CPU_REG_BYTE cpu_reg_byte_187 (
    .h(cpu_decoder_4x16_1_out_12), .v(cpu_decoder_4x16_2_out_6), .i(i), .o(cpu_reg_byte_1_o), .s(s), .e(e),
    .RESET(reset), .op(_164));
  CPU_REG_BYTE cpu_reg_byte_188 (
    .h(cpu_decoder_4x16_1_out_13), .v(cpu_decoder_4x16_2_out_6), .i(i), .o(cpu_reg_byte_1_o), .s(s), .e(e),
    .RESET(reset), .op(_180));
  CPU_REG_BYTE cpu_reg_byte_189 (
    .h(cpu_decoder_4x16_1_out_14), .v(cpu_decoder_4x16_2_out_6), .i(i), .o(cpu_reg_byte_1_o), .s(s), .e(e),
    .RESET(reset), .op(_196));
  CPU_REG_BYTE cpu_reg_byte_190 (
    .h(cpu_decoder_4x16_1_out_15), .v(cpu_decoder_4x16_2_out_6), .i(i), .o(cpu_reg_byte_1_o), .s(s), .e(e),
    .RESET(reset), .op(_212));
  CPU_REG_BYTE cpu_reg_byte_191 (
    .h(cpu_decoder_4x16_1_out_16), .v(cpu_decoder_4x16_2_out_6), .i(i), .o(cpu_reg_byte_1_o), .s(s), .e(e),
    .RESET(reset), .op(_228));
  CPU_REG_BYTE cpu_reg_byte_192 (
    .h(cpu_decoder_4x16_1_m), .v(cpu_decoder_4x16_2_out_6), .i(i), .o(cpu_reg_byte_1_o), .s(s), .e(e),
    .RESET(reset), .op(_244));
  CPU_REG_BYTE cpu_reg_byte_193 (
    .h(cpu_decoder_4x16_1_l), .v(cpu_decoder_4x16_2_out_5), .i(i), .o(cpu_reg_byte_1_o), .s(s), .e(e),
    .RESET(reset), .op(_3));
  CPU_REG_BYTE cpu_reg_byte_194 (
    .h(cpu_decoder_4x16_1_out_3), .v(cpu_decoder_4x16_2_out_5), .i(i), .o(cpu_reg_byte_1_o), .s(s), .e(e),
    .RESET(reset), .op(_19));
  CPU_REG_BYTE cpu_reg_byte_195 (
    .h(cpu_decoder_4x16_1_out_4), .v(cpu_decoder_4x16_2_out_5), .i(i), .o(cpu_reg_byte_1_o), .s(s), .e(e),
    .RESET(reset), .op(_35));
  CPU_REG_BYTE cpu_reg_byte_196 (
    .h(cpu_decoder_4x16_1_out_5), .v(cpu_decoder_4x16_2_out_5), .i(i), .o(cpu_reg_byte_1_o), .s(s), .e(e),
    .RESET(reset), .op(_51));
  CPU_REG_BYTE cpu_reg_byte_197 (
    .h(cpu_decoder_4x16_1_out_6), .v(cpu_decoder_4x16_2_out_5), .i(i), .o(cpu_reg_byte_1_o), .s(s), .e(e),
    .RESET(reset), .op(_67));
  CPU_REG_BYTE cpu_reg_byte_198 (
    .h(cpu_decoder_4x16_1_out_7), .v(cpu_decoder_4x16_2_out_5), .i(i), .o(cpu_reg_byte_1_o), .s(s), .e(e),
    .RESET(reset), .op(_83));
  CPU_REG_BYTE cpu_reg_byte_199 (
    .h(cpu_decoder_4x16_1_out_8), .v(cpu_decoder_4x16_2_out_5), .i(i), .o(cpu_reg_byte_1_o), .s(s), .e(e),
    .RESET(reset), .op(_99));
  CPU_REG_BYTE cpu_reg_byte_200 (
    .h(cpu_decoder_4x16_1_out_9), .v(cpu_decoder_4x16_2_out_5), .i(i), .o(cpu_reg_byte_1_o), .s(s), .e(e),
    .RESET(reset), .op(_115));
  CPU_REG_BYTE cpu_reg_byte_201 (
    .h(cpu_decoder_4x16_1_out_10), .v(cpu_decoder_4x16_2_out_5), .i(i), .o(cpu_reg_byte_1_o), .s(s), .e(e),
    .RESET(reset), .op(_131));
  CPU_REG_BYTE cpu_reg_byte_202 (
    .h(cpu_decoder_4x16_1_out_11), .v(cpu_decoder_4x16_2_out_5), .i(i), .o(cpu_reg_byte_1_o), .s(s), .e(e),
    .RESET(reset), .op(_147));
  CPU_REG_BYTE cpu_reg_byte_203 (
    .h(cpu_decoder_4x16_1_out_12), .v(cpu_decoder_4x16_2_out_5), .i(i), .o(cpu_reg_byte_1_o), .s(s), .e(e),
    .RESET(reset), .op(_163));
  CPU_REG_BYTE cpu_reg_byte_204 (
    .h(cpu_decoder_4x16_1_out_13), .v(cpu_decoder_4x16_2_out_5), .i(i), .o(cpu_reg_byte_1_o), .s(s), .e(e),
    .RESET(reset), .op(_179));
  CPU_REG_BYTE cpu_reg_byte_205 (
    .h(cpu_decoder_4x16_1_out_14), .v(cpu_decoder_4x16_2_out_5), .i(i), .o(cpu_reg_byte_1_o), .s(s), .e(e),
    .RESET(reset), .op(_195));
  CPU_REG_BYTE cpu_reg_byte_206 (
    .h(cpu_decoder_4x16_1_out_15), .v(cpu_decoder_4x16_2_out_5), .i(i), .o(cpu_reg_byte_1_o), .s(s), .e(e),
    .RESET(reset), .op(_211));
  CPU_REG_BYTE cpu_reg_byte_207 (
    .h(cpu_decoder_4x16_1_out_16), .v(cpu_decoder_4x16_2_out_5), .i(i), .o(cpu_reg_byte_1_o), .s(s), .e(e),
    .RESET(reset), .op(_227));
  CPU_REG_BYTE cpu_reg_byte_208 (
    .h(cpu_decoder_4x16_1_m), .v(cpu_decoder_4x16_2_out_5), .i(i), .o(cpu_reg_byte_1_o), .s(s), .e(e),
    .RESET(reset), .op(_243));
  CPU_REG_BYTE cpu_reg_byte_209 (
    .h(cpu_decoder_4x16_1_l), .v(cpu_decoder_4x16_2_out_4), .i(i), .o(cpu_reg_byte_1_o), .s(s), .e(e),
    .RESET(reset), .op(_2));
  CPU_REG_BYTE cpu_reg_byte_210 (
    .h(cpu_decoder_4x16_1_out_3), .v(cpu_decoder_4x16_2_out_4), .i(i), .o(cpu_reg_byte_1_o), .s(s), .e(e),
    .RESET(reset), .op(_18));
  CPU_REG_BYTE cpu_reg_byte_211 (
    .h(cpu_decoder_4x16_1_out_4), .v(cpu_decoder_4x16_2_out_4), .i(i), .o(cpu_reg_byte_1_o), .s(s), .e(e),
    .RESET(reset), .op(_34));
  CPU_REG_BYTE cpu_reg_byte_212 (
    .h(cpu_decoder_4x16_1_out_5), .v(cpu_decoder_4x16_2_out_4), .i(i), .o(cpu_reg_byte_1_o), .s(s), .e(e),
    .RESET(reset), .op(_50));
  CPU_REG_BYTE cpu_reg_byte_213 (
    .h(cpu_decoder_4x16_1_out_6), .v(cpu_decoder_4x16_2_out_4), .i(i), .o(cpu_reg_byte_1_o), .s(s), .e(e),
    .RESET(reset), .op(_66));
  CPU_REG_BYTE cpu_reg_byte_214 (
    .h(cpu_decoder_4x16_1_out_7), .v(cpu_decoder_4x16_2_out_4), .i(i), .o(cpu_reg_byte_1_o), .s(s), .e(e),
    .RESET(reset), .op(_82));
  CPU_REG_BYTE cpu_reg_byte_215 (
    .h(cpu_decoder_4x16_1_out_8), .v(cpu_decoder_4x16_2_out_4), .i(i), .o(cpu_reg_byte_1_o), .s(s), .e(e),
    .RESET(reset), .op(_98));
  CPU_REG_BYTE cpu_reg_byte_216 (
    .h(cpu_decoder_4x16_1_out_9), .v(cpu_decoder_4x16_2_out_4), .i(i), .o(cpu_reg_byte_1_o), .s(s), .e(e),
    .RESET(reset), .op(_114));
  CPU_REG_BYTE cpu_reg_byte_217 (
    .h(cpu_decoder_4x16_1_out_10), .v(cpu_decoder_4x16_2_out_4), .i(i), .o(cpu_reg_byte_1_o), .s(s), .e(e),
    .RESET(reset), .op(_130));
  CPU_REG_BYTE cpu_reg_byte_218 (
    .h(cpu_decoder_4x16_1_out_11), .v(cpu_decoder_4x16_2_out_4), .i(i), .o(cpu_reg_byte_1_o), .s(s), .e(e),
    .RESET(reset), .op(_146));
  CPU_REG_BYTE cpu_reg_byte_219 (
    .h(cpu_decoder_4x16_1_out_12), .v(cpu_decoder_4x16_2_out_4), .i(i), .o(cpu_reg_byte_1_o), .s(s), .e(e),
    .RESET(reset), .op(_162));
  CPU_REG_BYTE cpu_reg_byte_220 (
    .h(cpu_decoder_4x16_1_out_13), .v(cpu_decoder_4x16_2_out_4), .i(i), .o(cpu_reg_byte_1_o), .s(s), .e(e),
    .RESET(reset), .op(_178));
  CPU_REG_BYTE cpu_reg_byte_221 (
    .h(cpu_decoder_4x16_1_out_14), .v(cpu_decoder_4x16_2_out_4), .i(i), .o(cpu_reg_byte_1_o), .s(s), .e(e),
    .RESET(reset), .op(_194));
  CPU_REG_BYTE cpu_reg_byte_222 (
    .h(cpu_decoder_4x16_1_out_15), .v(cpu_decoder_4x16_2_out_4), .i(i), .o(cpu_reg_byte_1_o), .s(s), .e(e),
    .RESET(reset), .op(_210));
  CPU_REG_BYTE cpu_reg_byte_223 (
    .h(cpu_decoder_4x16_1_out_16), .v(cpu_decoder_4x16_2_out_4), .i(i), .o(cpu_reg_byte_1_o), .s(s), .e(e),
    .RESET(reset), .op(_226));
  CPU_REG_BYTE cpu_reg_byte_224 (
    .h(cpu_decoder_4x16_1_m), .v(cpu_decoder_4x16_2_out_4), .i(i), .o(cpu_reg_byte_1_o), .s(s), .e(e),
    .RESET(reset), .op(_242));
  CPU_REG_BYTE cpu_reg_byte_225 (
    .h(cpu_decoder_4x16_1_l), .v(cpu_decoder_4x16_2_out_3), .i(i), .o(cpu_reg_byte_1_o), .s(s), .e(e),
    .RESET(reset), .op(_1));
  CPU_REG_BYTE cpu_reg_byte_226 (
    .h(cpu_decoder_4x16_1_out_3), .v(cpu_decoder_4x16_2_out_3), .i(i), .o(cpu_reg_byte_1_o), .s(s), .e(e),
    .RESET(reset), .op(_17));
  CPU_REG_BYTE cpu_reg_byte_227 (
    .h(cpu_decoder_4x16_1_out_4), .v(cpu_decoder_4x16_2_out_3), .i(i), .o(cpu_reg_byte_1_o), .s(s), .e(e),
    .RESET(reset), .op(_33));
  CPU_REG_BYTE cpu_reg_byte_228 (
    .h(cpu_decoder_4x16_1_out_5), .v(cpu_decoder_4x16_2_out_3), .i(i), .o(cpu_reg_byte_1_o), .s(s), .e(e),
    .RESET(reset), .op(_49));
  CPU_REG_BYTE cpu_reg_byte_229 (
    .h(cpu_decoder_4x16_1_out_6), .v(cpu_decoder_4x16_2_out_3), .i(i), .o(cpu_reg_byte_1_o), .s(s), .e(e),
    .RESET(reset), .op(_65));
  CPU_REG_BYTE cpu_reg_byte_230 (
    .h(cpu_decoder_4x16_1_out_7), .v(cpu_decoder_4x16_2_out_3), .i(i), .o(cpu_reg_byte_1_o), .s(s), .e(e),
    .RESET(reset), .op(_81));
  CPU_REG_BYTE cpu_reg_byte_231 (
    .h(cpu_decoder_4x16_1_out_8), .v(cpu_decoder_4x16_2_out_3), .i(i), .o(cpu_reg_byte_1_o), .s(s), .e(e),
    .RESET(reset), .op(_97));
  CPU_REG_BYTE cpu_reg_byte_232 (
    .h(cpu_decoder_4x16_1_out_9), .v(cpu_decoder_4x16_2_out_3), .i(i), .o(cpu_reg_byte_1_o), .s(s), .e(e),
    .RESET(reset), .op(_113));
  CPU_REG_BYTE cpu_reg_byte_233 (
    .h(cpu_decoder_4x16_1_out_10), .v(cpu_decoder_4x16_2_out_3), .i(i), .o(cpu_reg_byte_1_o), .s(s), .e(e),
    .RESET(reset), .op(_129));
  CPU_REG_BYTE cpu_reg_byte_234 (
    .h(cpu_decoder_4x16_1_out_11), .v(cpu_decoder_4x16_2_out_3), .i(i), .o(cpu_reg_byte_1_o), .s(s), .e(e),
    .RESET(reset), .op(_145));
  CPU_REG_BYTE cpu_reg_byte_235 (
    .h(cpu_decoder_4x16_1_out_12), .v(cpu_decoder_4x16_2_out_3), .i(i), .o(cpu_reg_byte_1_o), .s(s), .e(e),
    .RESET(reset), .op(_161));
  CPU_REG_BYTE cpu_reg_byte_236 (
    .h(cpu_decoder_4x16_1_out_13), .v(cpu_decoder_4x16_2_out_3), .i(i), .o(cpu_reg_byte_1_o), .s(s), .e(e),
    .RESET(reset), .op(_177));
  CPU_REG_BYTE cpu_reg_byte_237 (
    .h(cpu_decoder_4x16_1_out_14), .v(cpu_decoder_4x16_2_out_3), .i(i), .o(cpu_reg_byte_1_o), .s(s), .e(e),
    .RESET(reset), .op(_193));
  CPU_REG_BYTE cpu_reg_byte_238 (
    .h(cpu_decoder_4x16_1_out_15), .v(cpu_decoder_4x16_2_out_3), .i(i), .o(cpu_reg_byte_1_o), .s(s), .e(e),
    .RESET(reset), .op(_209));
  CPU_REG_BYTE cpu_reg_byte_239 (
    .h(cpu_decoder_4x16_1_out_16), .v(cpu_decoder_4x16_2_out_3), .i(i), .o(cpu_reg_byte_1_o), .s(s), .e(e),
    .RESET(reset), .op(_225));
  CPU_REG_BYTE cpu_reg_byte_240 (
    .h(cpu_decoder_4x16_1_m), .v(cpu_decoder_4x16_2_out_3), .i(i), .o(cpu_reg_byte_1_o), .s(s), .e(e),
    .RESET(reset), .op(_241));
  CPU_REG_BYTE cpu_reg_byte_241 (
    .h(cpu_decoder_4x16_1_l), .v(cpu_decoder_4x16_2_l), .i(i), .o(cpu_reg_byte_1_o), .s(s), .e(e),
    .RESET(reset), .op(_0));
  CPU_REG_BYTE cpu_reg_byte_242 (
    .h(cpu_decoder_4x16_1_out_3), .v(cpu_decoder_4x16_2_l), .i(i), .o(cpu_reg_byte_1_o), .s(s), .e(e),
    .RESET(reset), .op(_16));
  CPU_REG_BYTE cpu_reg_byte_243 (
    .h(cpu_decoder_4x16_1_out_4), .v(cpu_decoder_4x16_2_l), .i(i), .o(cpu_reg_byte_1_o), .s(s), .e(e),
    .RESET(reset), .op(_32));
  CPU_REG_BYTE cpu_reg_byte_244 (
    .h(cpu_decoder_4x16_1_out_5), .v(cpu_decoder_4x16_2_l), .i(i), .o(cpu_reg_byte_1_o), .s(s), .e(e),
    .RESET(reset), .op(_48));
  CPU_REG_BYTE cpu_reg_byte_245 (
    .h(cpu_decoder_4x16_1_out_6), .v(cpu_decoder_4x16_2_l), .i(i), .o(cpu_reg_byte_1_o), .s(s), .e(e),
    .RESET(reset), .op(_64));
  CPU_REG_BYTE cpu_reg_byte_246 (
    .h(cpu_decoder_4x16_1_out_7), .v(cpu_decoder_4x16_2_l), .i(i), .o(cpu_reg_byte_1_o), .s(s), .e(e),
    .RESET(reset), .op(_80));
  CPU_REG_BYTE cpu_reg_byte_247 (
    .h(cpu_decoder_4x16_1_out_8), .v(cpu_decoder_4x16_2_l), .i(i), .o(cpu_reg_byte_1_o), .s(s), .e(e),
    .RESET(reset), .op(_96));
  CPU_REG_BYTE cpu_reg_byte_248 (
    .h(cpu_decoder_4x16_1_out_9), .v(cpu_decoder_4x16_2_l), .i(i), .o(cpu_reg_byte_1_o), .s(s), .e(e),
    .RESET(reset), .op(_112));
  CPU_REG_BYTE cpu_reg_byte_249 (
    .h(cpu_decoder_4x16_1_out_10), .v(cpu_decoder_4x16_2_l), .i(i), .o(cpu_reg_byte_1_o), .s(s), .e(e),
    .RESET(reset), .op(_128));
  CPU_REG_BYTE cpu_reg_byte_250 (
    .h(cpu_decoder_4x16_1_out_11), .v(cpu_decoder_4x16_2_l), .i(i), .o(cpu_reg_byte_1_o), .s(s), .e(e),
    .RESET(reset), .op(_144));
  CPU_REG_BYTE cpu_reg_byte_251 (
    .h(cpu_decoder_4x16_1_out_12), .v(cpu_decoder_4x16_2_l), .i(i), .o(cpu_reg_byte_1_o), .s(s), .e(e),
    .RESET(reset), .op(_160));
  CPU_REG_BYTE cpu_reg_byte_252 (
    .h(cpu_decoder_4x16_1_out_13), .v(cpu_decoder_4x16_2_l), .i(i), .o(cpu_reg_byte_1_o), .s(s), .e(e),
    .RESET(reset), .op(_176));
  CPU_REG_BYTE cpu_reg_byte_253 (
    .h(cpu_decoder_4x16_1_out_14), .v(cpu_decoder_4x16_2_l), .i(i), .o(cpu_reg_byte_1_o), .s(s), .e(e),
    .RESET(reset), .op(_192));
  CPU_REG_BYTE cpu_reg_byte_254 (
    .h(cpu_decoder_4x16_1_out_15), .v(cpu_decoder_4x16_2_l), .i(i), .o(cpu_reg_byte_1_o), .s(s), .e(e),
    .RESET(reset), .op(_208));
  CPU_REG_BYTE cpu_reg_byte_255 (
    .h(cpu_decoder_4x16_1_out_16), .v(cpu_decoder_4x16_2_l), .i(i), .o(cpu_reg_byte_1_o), .s(s), .e(e),
    .RESET(reset), .op(_224));
  CPU_REG_BYTE cpu_reg_byte_256 (
    .h(cpu_decoder_4x16_1_m), .v(cpu_decoder_4x16_2_l), .i(i), .o(cpu_reg_byte_1_o), .s(s), .e(e),
    .RESET(reset), .op(_240));

  // Notes on the sheet:
  //   o: pull=down
  //   _6: pull=up
  //   i: pull=down
  //   _3: pull=up
  //   address: pull=down
  //   _7: pull=up
  //   _4: pull=up
  //   _0: pull=down
  //   _2: pull=up
  //   sa: pull=down
endmodule

module CPU_NOT (
  input  [7:0] i,
  output [7:0] out_2
);

  not not_1 (out_2[0], i[0]);
  not not_2 (out_2[1], i[1]);
  not not_3 (out_2[2], i[2]);
  not not_4 (out_2[3], i[3]);
  not not_5 (out_2[4], i[4]);
  not not_6 (out_2[5], i[5]);
  not not_7 (out_2[6], i[6]);
  not not_8 (out_2[7], i[7]);
endmodule

module CPU_AND (
  input  [7:0] a,
  input  [7:0] b,
  output [7:0] o
);

  and and_1 (o[0], a[0], b[0]);
  and and_2 (o[1], a[1], b[1]);
  and and_3 (o[2], a[2], b[2]);
  and and_4 (o[3], a[3], b[3]);
  and and_5 (o[4], a[4], b[4]);
  and and_6 (o[5], a[5], b[5]);
  and and_7 (o[6], a[6], b[6]);
  and and_8 (o[7], a[7], b[7]);
endmodule

module CPU_OR (
  input  [7:0] a,
  input  [7:0] b,
  output [7:0] _0
);

  or or_1 (_0[0], a[0], b[0]);
  or or_2 (_0[1], a[1], b[1]);
  or or_3 (_0[2], a[2], b[2]);
  or or_4 (_0[3], a[3], b[3]);
  or or_5 (_0[4], a[4], b[4]);
  or or_6 (_0[5], a[5], b[5]);
  or or_7 (_0[6], a[6], b[6]);
  or or_8 (_0[7], a[7], b[7]);
endmodule

module CPU_XOR_1 (
  input  a,
  input  b,
  output o
);

  wire nand_1_out, nand_2_out, not_1_out, not_2_out;

  not not_1 (not_1_out, a);
  not not_2 (not_2_out, b);
  nand nand_1 (nand_1_out, not_1_out, b);
  nand nand_2 (nand_2_out, a, not_2_out);
  nand nand_3 (o, nand_1_out, nand_2_out);
endmodule

module CPU_SHR (
  input  [7:0] i,
  input  shift_in,
  output shift_out,
  output [7:0] o
);

  wire [7:1] cpu_register_8_1__0;

  CPU_REGISTER_8 cpu_register_8_1 (.i(i), .s(1'b1), .e(1'b1), ._0({cpu_register_8_1__0, shift_out}));  // open: REG
  CPU_REGISTER_8 cpu_register_8_2 (.i({shift_in, cpu_register_8_1__0}), .s(1'b1), .e(1'b1), ._0(o));  // open: REG
endmodule

module CPU_SHL (
  input  shift_in,
  input  [7:0] i,
  output [7:0] o,
  output shift_out
);

  wire [6:0] cpu_register_8_1__0;

  CPU_REGISTER_8 cpu_register_8_1 (.i(i), .s(1'b1), .e(1'b1), ._0({shift_out, cpu_register_8_1__0}));  // open: REG
  CPU_REGISTER_8 cpu_register_8_2 (.i({cpu_register_8_1__0, shift_in}), .s(1'b1), .e(1'b1), ._0(o));  // open: REG
endmodule

module CPU_ADDER (
  input  a,
  input  b,
  input  carry_in,
  output sum,
  output carry_out
);

  wire and_1_out, and_2_out, cpu_xor_1_1_o;

  CPU_XOR_1 cpu_xor_1_1 (.a(a), .b(b), .o(cpu_xor_1_1_o));
  and and_1 (and_1_out, carry_in, cpu_xor_1_1_o);
  and and_2 (and_2_out, a, b);
  CPU_XOR_1 cpu_xor_1_2 (.a(cpu_xor_1_1_o), .b(carry_in), .o(sum));
  or or_1 (carry_out, and_1_out, and_2_out);
endmodule

module CPU_ADDER_8 (
  input  [7:0] a,
  input  [7:0] b,
  input  carry_in,
  output carry_out,
  output [7:0] out_5
);

  wire cpu_adder_2_carry_out, cpu_adder_3_carry_out, cpu_adder_4_carry_out, cpu_adder_5_carry_out,
       cpu_adder_6_carry_out, cpu_adder_7_carry_out, cpu_adder_8_carry_out;

  CPU_ADDER cpu_adder_1 (.a(a[7]), .b(b[7]), .carry_in(cpu_adder_2_carry_out), .sum(out_5[7]), .carry_out(carry_out));
  CPU_ADDER cpu_adder_2 (
    .a(a[6]), .b(b[6]), .carry_in(cpu_adder_3_carry_out), .sum(out_5[6]), .carry_out(cpu_adder_2_carry_out));
  CPU_ADDER cpu_adder_3 (
    .a(a[5]), .b(b[5]), .carry_in(cpu_adder_4_carry_out), .sum(out_5[5]), .carry_out(cpu_adder_3_carry_out));
  CPU_ADDER cpu_adder_4 (
    .a(a[4]), .b(b[4]), .carry_in(cpu_adder_5_carry_out), .sum(out_5[4]), .carry_out(cpu_adder_4_carry_out));
  CPU_ADDER cpu_adder_5 (
    .a(a[3]), .b(b[3]), .carry_in(cpu_adder_6_carry_out), .sum(out_5[3]), .carry_out(cpu_adder_5_carry_out));
  CPU_ADDER cpu_adder_6 (
    .a(a[2]), .b(b[2]), .carry_in(cpu_adder_7_carry_out), .sum(out_5[2]), .carry_out(cpu_adder_6_carry_out));
  CPU_ADDER cpu_adder_7 (
    .a(a[1]), .b(b[1]), .carry_in(cpu_adder_8_carry_out), .sum(out_5[1]), .carry_out(cpu_adder_7_carry_out));
  CPU_ADDER cpu_adder_8 (.a(a[0]), .b(b[0]), .carry_in(carry_in), .sum(out_5[0]), .carry_out(cpu_adder_8_carry_out));
endmodule

module CPU_XOR_LE_1 (
  input  above_equal,
  input  a_larger,
  input  a,
  input  b,
  output c,
  output equal,
  output a_large
);

  wire and_2_out, not_1_out;

  CPU_XOR_1 cpu_xor_1_1 (.a(a), .b(b), .o(c));
  not not_1 (not_1_out, c);
  and and_1 (equal, not_1_out, above_equal);
  and and_2 (and_2_out, above_equal, a, c);
  or or_1 (a_large, and_2_out, a_larger);
endmodule

module CPU_XOR_LE_8 (
  input  [7:0] a,
  input  [7:0] b,
  output [7:0] out_3,
  output larger,
  output equal
);

  wire cpu_xor_le_1_1_a_large, cpu_xor_le_1_1_equal, cpu_xor_le_1_2_a_large, cpu_xor_le_1_2_equal,
       cpu_xor_le_1_3_a_large, cpu_xor_le_1_3_equal, cpu_xor_le_1_4_a_large, cpu_xor_le_1_4_equal,
       cpu_xor_le_1_5_a_large, cpu_xor_le_1_5_equal, cpu_xor_le_1_6_a_large, cpu_xor_le_1_6_equal,
       cpu_xor_le_1_7_a_large, cpu_xor_le_1_7_equal;

  CPU_XOR_LE_1 cpu_xor_le_1_1 (
    .a(a[0]), .b(b[0]), .a_larger(1'b0), .c(out_3[0]), .above_equal(1'b1), .equal(cpu_xor_le_1_1_equal),
    .a_large(cpu_xor_le_1_1_a_large));
  CPU_XOR_LE_1 cpu_xor_le_1_2 (
    .a(a[1]), .b(b[1]), .a_larger(cpu_xor_le_1_1_a_large), .c(out_3[1]), .above_equal(cpu_xor_le_1_1_equal),
    .equal(cpu_xor_le_1_2_equal), .a_large(cpu_xor_le_1_2_a_large));
  CPU_XOR_LE_1 cpu_xor_le_1_3 (
    .a(a[2]), .b(b[2]), .a_larger(cpu_xor_le_1_2_a_large), .c(out_3[2]), .above_equal(cpu_xor_le_1_2_equal),
    .equal(cpu_xor_le_1_3_equal), .a_large(cpu_xor_le_1_3_a_large));
  CPU_XOR_LE_1 cpu_xor_le_1_4 (
    .a(a[3]), .b(b[3]), .a_larger(cpu_xor_le_1_3_a_large), .c(out_3[3]), .above_equal(cpu_xor_le_1_3_equal),
    .equal(cpu_xor_le_1_4_equal), .a_large(cpu_xor_le_1_4_a_large));
  CPU_XOR_LE_1 cpu_xor_le_1_5 (
    .a(a[4]), .b(b[4]), .a_larger(cpu_xor_le_1_4_a_large), .c(out_3[4]), .above_equal(cpu_xor_le_1_4_equal),
    .equal(cpu_xor_le_1_5_equal), .a_large(cpu_xor_le_1_5_a_large));
  CPU_XOR_LE_1 cpu_xor_le_1_6 (
    .a(a[5]), .b(b[5]), .a_larger(cpu_xor_le_1_5_a_large), .c(out_3[5]), .above_equal(cpu_xor_le_1_5_equal),
    .equal(cpu_xor_le_1_6_equal), .a_large(cpu_xor_le_1_6_a_large));
  CPU_XOR_LE_1 cpu_xor_le_1_7 (
    .a(a[6]), .b(b[6]), .a_larger(cpu_xor_le_1_6_a_large), .c(out_3[6]), .above_equal(cpu_xor_le_1_6_equal),
    .equal(cpu_xor_le_1_7_equal), .a_large(cpu_xor_le_1_7_a_large));
  CPU_XOR_LE_1 cpu_xor_le_1_8 (
    .a(a[7]), .b(b[7]), .a_larger(cpu_xor_le_1_7_a_large), .c(out_3[7]), .above_equal(cpu_xor_le_1_7_equal),
    .equal(equal), .a_large(larger));
endmodule

module CPU_Z (
  input  [7:0] i,
  output o
);

  wire or_1_out;

  or or_1 (or_1_out, i[0], i[1], i[2], i[3], i[4], i[5], i[6], i[7]);
  not not_1 (o, or_1_out);
endmodule

module CPU_DECODER_3x8 (
  input  c,
  input  b,
  input  a,
  output [7:0] o
);

  wire not_1_out, not_2_out, not_3_out;

  not not_1 (not_1_out, a);
  not not_2 (not_2_out, b);
  not not_3 (not_3_out, c);
  and and_1 (o[0], not_3_out, not_2_out, not_1_out);
  and and_2 (o[1], not_3_out, not_2_out, a);
  and and_3 (o[2], not_3_out, b, not_1_out);
  and and_4 (o[3], not_3_out, b, a);
  and and_5 (o[4], c, not_2_out, not_1_out);
  and and_6 (o[5], c, not_2_out, a);
  and and_7 (o[6], c, b, not_1_out);
  and and_8 (o[7], c, b, a);

  // Notes on the sheet:
  //   o: pull=down
  //   b: pull=down
  //   a: pull=down
  //   c: pull=down
  //   msb
  //   lsb
endmodule

module CPU_E (
  input  [7:0] in_1,
  input  in_2,
  output [7:0] out_3
);

  wire and_1_out, and_2_out, and_3_out, and_4_out, and_5_out, and_6_out, and_7_out, and_8_out;

  assign out_3[0] = in_2 ? and_1_out : 1'bz;  // Controlled_Buffer controlled_buffer_1
  and and_1 (and_1_out, in_1[0], in_2);
  assign out_3[1] = in_2 ? and_2_out : 1'bz;  // Controlled_Buffer controlled_buffer_2
  and and_2 (and_2_out, in_1[1], in_2);
  and and_3 (and_3_out, in_1[2], in_2);
  assign out_3[2] = in_2 ? and_3_out : 1'bz;  // Controlled_Buffer controlled_buffer_3
  assign out_3[3] = in_2 ? and_4_out : 1'bz;  // Controlled_Buffer controlled_buffer_4
  and and_4 (and_4_out, in_1[3], in_2);
  assign out_3[4] = in_2 ? and_5_out : 1'bz;  // Controlled_Buffer controlled_buffer_5
  and and_5 (and_5_out, in_1[4], in_2);
  assign out_3[5] = in_2 ? and_6_out : 1'bz;  // Controlled_Buffer controlled_buffer_6
  and and_6 (and_6_out, in_1[5], in_2);
  and and_7 (and_7_out, in_1[6], in_2);
  assign out_3[6] = in_2 ? and_7_out : 1'bz;  // Controlled_Buffer controlled_buffer_7
  and and_8 (and_8_out, in_1[7], in_2);
  assign out_3[7] = in_2 ? and_8_out : 1'bz;  // Controlled_Buffer controlled_buffer_8
endmodule

module CPU_ALU (
  input  [7:0] a,
  input  [7:0] b,
  input  carry_in,
  input  a_2,
  input  b_2,
  input  c,
  output a_larger,
  output equal,
  output zero,
  output [7:0] c_2,
  output carry_out
);

  wire and_1_out, and_2_out, and_3_out, cpu_adder_8_1_carry_out, cpu_shl_1_shift_out, cpu_shr_1_shift_out;
  wire [7:0] cpu_adder_8_1_out_5, cpu_and_1_o, cpu_decoder_3x8_1_o, cpu_not_1_out_2, cpu_or_1__0,
       cpu_shl_1_o, cpu_shr_1_o, cpu_xor_le_8_1_out_3;

  CPU_XOR_LE_8 cpu_xor_le_8_1 (.a(a), .b(b), .out_3(cpu_xor_le_8_1_out_3), .larger(a_larger), .equal(equal));
  CPU_AND cpu_and_1 (.a(a), .o(cpu_and_1_o), .b(b));
  CPU_NOT cpu_not_1 (.i(a), .out_2(cpu_not_1_out_2));
  CPU_SHL cpu_shl_1 (.shift_in(carry_in), .i(a), .o(cpu_shl_1_o), .shift_out(cpu_shl_1_shift_out));
  CPU_SHR cpu_shr_1 (.shift_out(cpu_shr_1_shift_out), .i(a), .o(cpu_shr_1_o), .shift_in(carry_in));
  CPU_ADDER_8 cpu_adder_8_1 (
    .a(a), .b(b), .carry_out(cpu_adder_8_1_carry_out), .out_5(cpu_adder_8_1_out_5), .carry_in(carry_in));
  CPU_OR cpu_or_1 (.a(a), .b(b), ._0(cpu_or_1__0));
  CPU_DECODER_3x8 cpu_decoder_3x8_1 (.b(b_2), .o(cpu_decoder_3x8_1_o), .c(c), .a(a_2));
  CPU_E cpu_e_1 (.in_1(cpu_xor_le_8_1_out_3), .out_3(c_2), .in_2(cpu_decoder_3x8_1_o[6]));
  CPU_E cpu_e_2 (.in_1(cpu_or_1__0), .out_3(c_2), .in_2(cpu_decoder_3x8_1_o[5]));
  CPU_E cpu_e_3 (.in_1(cpu_and_1_o), .out_3(c_2), .in_2(cpu_decoder_3x8_1_o[4]));
  CPU_E cpu_e_4 (.in_1(cpu_not_1_out_2), .out_3(c_2), .in_2(cpu_decoder_3x8_1_o[3]));
  CPU_E cpu_e_5 (.in_1(cpu_shl_1_o), .out_3(c_2), .in_2(cpu_decoder_3x8_1_o[2]));
  CPU_E cpu_e_6 (.in_1(cpu_shr_1_o), .out_3(c_2), .in_2(cpu_decoder_3x8_1_o[1]));
  CPU_E cpu_e_7 (.in_1(cpu_adder_8_1_out_5), .out_3(c_2), .in_2(cpu_decoder_3x8_1_o[0]));
  assign carry_out = cpu_decoder_3x8_1_o[2] ? and_1_out : 1'bz;  // Controlled_Buffer controlled_buffer_1
  and and_1 (and_1_out, cpu_shl_1_shift_out, cpu_decoder_3x8_1_o[2]);
  assign carry_out = cpu_decoder_3x8_1_o[1] ? and_2_out : 1'bz;  // Controlled_Buffer controlled_buffer_2
  and and_2 (and_2_out, cpu_shr_1_shift_out, cpu_decoder_3x8_1_o[1]);
  and and_3 (and_3_out, cpu_adder_8_1_carry_out, cpu_decoder_3x8_1_o[0]);
  assign carry_out = cpu_decoder_3x8_1_o[0] ? and_3_out : 1'bz;  // Controlled_Buffer controlled_buffer_3
  CPU_Z cpu_z_1 (.i(c_2), .o(zero));

  // Notes on the sheet:
  //   carry_in: pull=down
  //   c_2: pull=down
  //   a_larger: pull=down
  //   b: pull=down
  //   equal: pull=down
  //   a_2: pull=down
  //   b_2: pull=down
  //   carry_out: pull=down
  //   zero: pull=down
  //   a: pull=down
  //   c: pull=down
endmodule

module CPU_BUS_1 (
  input  [7:0] i,
  input  bus_1,
  output [7:0] o
);

  wire not_1_out;

  and and_1 (o[7], i[7], not_1_out);
  and and_2 (o[6], i[6], not_1_out);
  and and_3 (o[5], i[5], not_1_out);
  and and_4 (o[3], i[3], not_1_out);
  and and_5 (o[4], i[4], not_1_out);
  and and_6 (o[2], i[2], not_1_out);
  and and_7 (o[1], i[1], not_1_out);
  not not_1 (not_1_out, bus_1);
  or or_1 (o[0], i[0], bus_1);

  // Notes on the sheet:
  //   o: pull=down
  //   bus_1: pull=down
  //   i: pull=down
endmodule

module CPU_ACCUMULATOR (
  input  [7:0] i,
  input  s,
  input  e,
  output [7:0] ACC,
  output [7:0] o
);

  CPU_REGISTER_8 cpu_register_8_1 (.i(i), .s(s), .e(e), ._0(o), .REG(ACC));

  // Notes on the sheet:
  //   o: pull=down
  //   i: pull=down
  //   s: pull=down
  //   e: pull=down
endmodule

module CPU_R (
  input  [7:0] i,
  input  s,
  input  e,
  output [7:0] \reg ,
  output [7:0] o
);

  CPU_REGISTER_8 cpu_register_8_1 (.i(i), .s(s), .e(e), ._0(o), .REG(\reg ));

  // Notes on the sheet:
  //   i: pull=down
  //   s: pull=down
  //   e: pull=down
  //   o: pull=down
endmodule

module CPU_TMP (
  input  [7:0] i,
  input  s,
  output [7:0] o
);

  wire [7:0] controlled_buffer_1_out;

  assign controlled_buffer_1_out = s ? i : 8'bz;  // Controlled_Buffer controlled_buffer_1
  CPU_MEM_8 cpu_mem_8_1 (.s(s), .in_1(controlled_buffer_1_out), .out_3(o));

  // Notes on the sheet:
  //   s: pull=down
  //   i: pull=down
  //   o: pull=down
endmodule

module CPU_STEPPER (
  input  reset,
  input  clk,
  output step_1,
  output step_2,
  output step_3,
  output step_4,
  output step_5,
  output step_6,
  output step_7
);

  wire cpu_mem_1_1_out_3, cpu_mem_1_2_out_3, cpu_mem_1_3_out_3, cpu_mem_1_4_out_3, cpu_mem_1_5_out_3,
       cpu_mem_1_6_out_3, cpu_mem_1_7_out_3, cpu_mem_1_8_out_3, cpu_mem_1_9_out_3, cpu_mem_1_10_out_3,
       cpu_mem_1_11_out_3, not_1_out, not_2_out, not_3_out, not_4_out, not_5_out, not_6_out, not_7_out,
       not_8_out, or_1_out, or_2_out;

  not not_1 (not_1_out, clk);
  not not_2 (not_2_out, reset);
  or or_1 (or_1_out, reset, clk);
  or or_2 (or_2_out, reset, not_1_out);
  or or_3 (step_1, reset, not_3_out);
  CPU_MEM_1 cpu_mem_1_1 (.in_1(not_2_out), .in_2(or_1_out), .out_3(cpu_mem_1_1_out_3));
  not not_3 (not_3_out, cpu_mem_1_2_out_3);
  CPU_MEM_1 cpu_mem_1_2 (.in_1(cpu_mem_1_1_out_3), .in_2(or_2_out), .out_3(cpu_mem_1_2_out_3));
  and and_1 (step_2, cpu_mem_1_2_out_3, not_4_out);
  not not_4 (not_4_out, cpu_mem_1_4_out_3);
  CPU_MEM_1 cpu_mem_1_3 (.in_1(cpu_mem_1_2_out_3), .in_2(or_1_out), .out_3(cpu_mem_1_3_out_3));
  CPU_MEM_1 cpu_mem_1_4 (.in_1(cpu_mem_1_3_out_3), .in_2(or_2_out), .out_3(cpu_mem_1_4_out_3));
  and and_2 (step_3, cpu_mem_1_4_out_3, not_5_out);
  CPU_MEM_1 cpu_mem_1_5 (.in_1(cpu_mem_1_4_out_3), .in_2(or_1_out), .out_3(cpu_mem_1_5_out_3));
  not not_5 (not_5_out, cpu_mem_1_6_out_3);
  CPU_MEM_1 cpu_mem_1_6 (.in_1(cpu_mem_1_5_out_3), .in_2(or_2_out), .out_3(cpu_mem_1_6_out_3));
  and and_3 (step_4, cpu_mem_1_6_out_3, not_6_out);
  not not_6 (not_6_out, cpu_mem_1_8_out_3);
  CPU_MEM_1 cpu_mem_1_7 (.in_1(cpu_mem_1_6_out_3), .in_2(or_1_out), .out_3(cpu_mem_1_7_out_3));
  and and_4 (step_5, cpu_mem_1_8_out_3, not_7_out);
  CPU_MEM_1 cpu_mem_1_8 (.in_1(cpu_mem_1_7_out_3), .in_2(or_2_out), .out_3(cpu_mem_1_8_out_3));
  CPU_MEM_1 cpu_mem_1_9 (.in_1(cpu_mem_1_8_out_3), .in_2(or_1_out), .out_3(cpu_mem_1_9_out_3));
  not not_7 (not_7_out, cpu_mem_1_10_out_3);
  CPU_MEM_1 cpu_mem_1_10 (.in_1(cpu_mem_1_9_out_3), .in_2(or_2_out), .out_3(cpu_mem_1_10_out_3));
  and and_5 (step_6, cpu_mem_1_10_out_3, not_8_out);
  CPU_MEM_1 cpu_mem_1_11 (.in_1(cpu_mem_1_10_out_3), .in_2(or_1_out), .out_3(cpu_mem_1_11_out_3));
  not not_8 (not_8_out, step_7);
  CPU_MEM_1 cpu_mem_1_12 (.in_1(cpu_mem_1_11_out_3), .in_2(or_2_out), .out_3(step_7));

  // Notes on the sheet:
  //   reset: pull=down
endmodule

module CPU (
  input  clock,
  input  LOAD,
  input  MARS,
  input  [7:0] RAM_INPUT,
  input  RESET,
  output [7:0] R0,
  output [7:0] R1,
  output [7:0] R2,
  output [7:0] R3,
  output clkl,
  output clke,
  output clks,
  output END,
  output S,
  output E,
  output IO,
  output DA,
  output [7:0] out_18,
  output [7:0] out_19,
  output [7:0] out_20,
  output [7:0] BUS_OUTPUT
);

  wire and_1_out, and_2_out, and_3_out, C, cpu_alu_1_a_larger, cpu_alu_1_carry_out, cpu_alu_1_equal,
       cpu_alu_1_zero, cpu_carry_temp_1_o, cpu_control_section_1_acc_e, cpu_control_section_1_acc_s,
       cpu_control_section_1_alu_0, cpu_control_section_1_alu_1, cpu_control_section_1_alu_2,
       cpu_control_section_1_bus_1, cpu_control_section_1_flags_s, cpu_control_section_1_iar_e,
       cpu_control_section_1_iar_s, cpu_control_section_1_ir_s, cpu_control_section_1_mar_s,
       cpu_control_section_1_r0_e, cpu_control_section_1_r0_s, cpu_control_section_1_r1_e,
       cpu_control_section_1_r1_s, cpu_control_section_1_r2_e, cpu_control_section_1_r2_s,
       cpu_control_section_1_r3_e, cpu_control_section_1_r3_s, cpu_control_section_1_ram_e,
       cpu_control_section_1_ram_s, cpu_flags_1_a_2, cpu_flags_1_c_2, cpu_flags_1_e_2, cpu_flags_1_z_2,
       not_1_out, S_t;
  wire [7:0] cpu_alu_1_c_2, cpu_bus_1_1_o, cpu_ram_256_1__56, cpu_tmp_1_o, load_256_count_1_count,
       multiplexer_1_out;

  CPU_ACCUMULATOR cpu_accumulator_1 (
    .i(cpu_alu_1_c_2), .o(BUS_OUTPUT), .s(cpu_control_section_1_acc_s), .e(cpu_control_section_1_acc_e),
    .ACC(out_20));
  CPU_TMP cpu_tmp_1 (.i(BUS_OUTPUT), .o(cpu_tmp_1_o), .s(S_t));
  CPU_BUS_1 cpu_bus_1_1 (.i(cpu_tmp_1_o), .bus_1(cpu_control_section_1_bus_1), .o(cpu_bus_1_1_o));
  CPU_ALU cpu_alu_1 (
    .a(BUS_OUTPUT), .b(cpu_bus_1_1_o), .carry_in(and_2_out), .a_2(cpu_control_section_1_alu_0),
    .b_2(cpu_control_section_1_alu_1), .c(cpu_control_section_1_alu_2), .zero(cpu_alu_1_zero),
    .c_2(cpu_alu_1_c_2), .carry_out(cpu_alu_1_carry_out), .a_larger(cpu_alu_1_a_larger),
    .equal(cpu_alu_1_equal));
  not not_1 (not_1_out, END);
  and and_1 (and_1_out, clock, not_1_out);
  and and_2 (and_2_out, cpu_carry_temp_1_o, C);
  and and_3 (and_3_out, LOAD, clkl);
  CPU_CLK cpu_clk_1 (.clkin(and_1_out), .clks(clks), .clke(clke), .clk(clkl));
  CPU_CARRY_TEMP cpu_carry_temp_1 (.c(cpu_flags_1_c_2), .o(cpu_carry_temp_1_o), .s(S_t));
  CPU_FLAGS cpu_flags_1 (
    .C(cpu_alu_1_carry_out), .A(cpu_alu_1_a_larger), .E(cpu_alu_1_equal), .Z(cpu_alu_1_zero),
    .C_2(cpu_flags_1_c_2), .A_2(cpu_flags_1_a_2), .E_2(cpu_flags_1_e_2), .Z_2(cpu_flags_1_z_2),
    .s(cpu_control_section_1_flags_s));
  LOAD_256_COUNT load_256_count_1 (.count(load_256_count_1_count), .clk(and_3_out));  // open: carry
  assign BUS_OUTPUT = LOAD ? load_256_count_1_count : 8'bz;  // Controlled_Buffer controlled_buffer_1
  CPU_CONTROL_SECTION cpu_control_section_1 (
    .clks(clks), .clke(clke), .clk(clkl), .MAR_S(cpu_control_section_1_mar_s),
    .ACC_S(cpu_control_section_1_acc_s), .TMP_S(S_t), .FLAGS_S(cpu_control_section_1_flags_s),
    .RAM_S(cpu_control_section_1_ram_s), .IO_CLKS_S(S), .IAR_E(cpu_control_section_1_iar_e),
    .RAM_E(cpu_control_section_1_ram_e), .IO_CLK_E(E), .BUS_1(cpu_control_section_1_bus_1),
    .ACC_E(cpu_control_section_1_acc_e), .IR_S(cpu_control_section_1_ir_s),
    .IAR_S(cpu_control_section_1_iar_s), .R0_S(cpu_control_section_1_r0_s),
    .R1_S(cpu_control_section_1_r1_s), .R2_S(cpu_control_section_1_r2_s), .R3_S(cpu_control_section_1_r3_s),
    .R0_E(cpu_control_section_1_r0_e), .R1_E(cpu_control_section_1_r1_e), .R2_E(cpu_control_section_1_r2_e),
    .R3_E(cpu_control_section_1_r3_e), .IR_IN(out_18), .ALU_0(cpu_control_section_1_alu_0),
    .ALU_1(cpu_control_section_1_alu_1), .ALU_2(cpu_control_section_1_alu_2), .C(cpu_flags_1_c_2),
    .A(cpu_flags_1_a_2), .E(cpu_flags_1_e_2), .Z(cpu_flags_1_z_2), .IO(IO), .DA(DA), .RESET(RESET), .C_2(C),
    .LOAD(LOAD), .END(END), .MARS(MARS));
  CPU_R cpu_r_1 (
    .i(BUS_OUTPUT), .o(BUS_OUTPUT), .s(cpu_control_section_1_r0_s), .e(cpu_control_section_1_r0_e), .\reg (R0));
  CPU_R cpu_r_2 (
    .i(BUS_OUTPUT), .o(BUS_OUTPUT), .s(cpu_control_section_1_r1_s), .e(cpu_control_section_1_r1_e), .\reg (R1));
  CPU_IAR cpu_iar_1 (
    .i(BUS_OUTPUT), .o(BUS_OUTPUT), .s(cpu_control_section_1_iar_s), .e(cpu_control_section_1_iar_e),
    .IAR(out_19));
  CPU_R cpu_r_3 (
    .i(BUS_OUTPUT), .o(BUS_OUTPUT), .s(cpu_control_section_1_r2_s), .e(cpu_control_section_1_r2_e), .\reg (R2));
  CPU_IR cpu_ir_1 (.i(BUS_OUTPUT), .o(out_18), .s(cpu_control_section_1_ir_s));
  CPU_R cpu_r_4 (
    .i(BUS_OUTPUT), .o(BUS_OUTPUT), .s(cpu_control_section_1_r3_s), .e(cpu_control_section_1_r3_e), .\reg (R3));
  Multiplexer #(.width(8)) multiplexer_1 (
    .in0(BUS_OUTPUT), .in1(RAM_INPUT), .out(multiplexer_1_out), .sel(LOAD));  // open: en
  CPU_RAM_256 cpu_ram_256_1 (
    .o(BUS_OUTPUT), .sa(cpu_control_section_1_mar_s), .address(BUS_OUTPUT), .s(cpu_control_section_1_ram_s),
    .e(cpu_control_section_1_ram_e), .i(multiplexer_1_out), .reset(RESET), ._56(cpu_ram_256_1__56),
    ._55(cpu_ram_256_1__56));  // open: _0, _2, _4, _6, _7, _8, _9, _10, _11, _12, _13, _14, _15, _31, _30, _29, _28, _27, _26, _25, _24, _23, _22, _21, _20, _19, _18, _17, _16, _46, _47, _45, _44, _43, _42, _41, _40, _39, _38, _37, _36, _35, _34, _32, _63, _62, _61, _60, _59, _58, _57, _54, _53, _52, _51, _50, _49, _48, _5, _1, _79, _78, _74, _77, _76, _75, _73, _72, _71, _70, _69, _68, _67, _66, _65, _64, _109, _108, _107, _106, _105, _111, _110, _104, _103, _102, _101, _100, _99, _98, _97, _96, _95, _94, _93, _92, _91, _90, _89, _88, _87, _86, _84, _83, _82, _81, _80, _85, _143, _142, _141, _140, _139, _138, _137, _136, _135, _134, _133, _132, _131, _130, _129, _128, _127, _126, _125, _124, _123, _122, _121, _120, _119, _118, _117, _116, _115, _114, _113, _112, _3, _159, _158, _157, _156, _155, _154, _153, _152, _151, _150, _149, _148, _147, _146, _145, _144, _33, _191, _190, _189, _188, _187, _186, _185, _184, _183, _182, _181, _180, _179, _178, _177, _176, _175, _174, _173, _172, _171, _170, _169, _168, _167, _166, _165, _164, _163, _162, _161, _160, _239, _238, _237, _236, _235, _234, _233, _232, _231, _230, _229, _228, _227, _226, _225, _224, _255, _254, _253, _252, _251, _250, _249, _248, _247, _246, _245, _244, _243, _242, _241, _240, _223, _222, _221, _220, _219, _218, _217, _216, _215, _214, _213, _212, _211, _210, _209, _208, _207, _206, _205, _204, _203, _202, _201, _200, _199, _198, _197, _196, _195, _194, _193, _192

  // Notes on the sheet:
  //   BUS_OUTPUT: pull=down
endmodule

module CPU_IAR (
  input  [7:0] i,
  input  s,
  input  e,
  output [7:0] IAR,
  output [7:0] o
);

  CPU_REGISTER_8 cpu_register_8_1 (.i(i), .s(s), .e(e), ._0(o), .REG(IAR));

  // Notes on the sheet:
  //   i: pull=down
  //   s: pull=down
  //   o: pull=down
  //   e: pull=down
endmodule

module CPU_IR (
  input  [7:0] i,
  input  s,
  output [7:0] o
);

  CPU_MEM_8 cpu_mem_8_1 (.s(s), .in_1(i), .out_3(o));

  // Notes on the sheet:
  //   o: pull=down
  //   s: pull=down
  //   i: pull=down
endmodule

module CPU_FLAGS (
  input  C,
  input  A,
  input  E,
  input  Z,
  input  s,
  output C_2,
  output A_2,
  output E_2,
  output Z_2
);

  CPU_MEM_1 cpu_mem_1_1 (.in_1(C), .in_2(s), .out_3(C_2));
  CPU_MEM_1 cpu_mem_1_2 (.in_1(A), .in_2(s), .out_3(A_2));
  CPU_MEM_1 cpu_mem_1_3 (.in_1(E), .in_2(s), .out_3(E_2));
  CPU_MEM_1 cpu_mem_1_4 (.in_1(Z), .in_2(s), .out_3(Z_2));

  // Notes on the sheet:
  //   E: pull=down
  //   E_2: pull=down
  //   Z_2: pull=down
  //   A: pull=down
  //   A_2: pull=down
  //   C: pull=down
  //   C_2: pull=down
  //   Z: pull=down
endmodule

module CPU_CONTROL_SECTION (
  input  clks,
  input  clk,
  input  clke,
  input  LOAD,
  input  MARS,
  input  RESET,
  input  C,
  input  A,
  input  E,
  input  Z,
  input  [7:0] IR_IN,
  output BUS_1,
  output IR_S,
  output MAR_S,
  output IAR_E,
  output IAR_S,
  output RAM_E,
  output ACC_S,
  output ACC_E,
  output RAM_S,
  output C_2,
  output TMP_S,
  output IO_CLK_E,
  output FLAGS_S,
  output IO_CLKS_S,
  output R0_S,
  output R0_E,
  output R1_S,
  output R1_E,
  output R2_E,
  output R2_S,
  output R3_E,
  output R3_S,
  output END,
  output IO,
  output DA,
  output ALU_0,
  output ALU_1,
  output ALU_2
);

  wire and_5_out, and_6_out, and_7_out, and_8_out, and_9_out, and_10_out, and_11_out, and_12_out, and_16_out,
       and_17_out, and_18_out, and_19_out, and_20_out, and_21_out, and_22_out, and_23_out, and_24_out,
       and_25_out, and_26_out, and_27_out, and_28_out, and_29_out, and_30_out, and_31_out, and_32_out,
       and_33_out, and_34_out, and_35_out, and_36_out, and_37_out, and_38_out, and_39_out, and_42_out,
       and_43_out, and_44_out, and_45_out, and_46_out, and_47_out, and_48_out, and_49_out, and_50_out,
       and_51_out, and_52_out, and_53_out, and_54_out, and_55_out, and_56_out, and_57_out, and_58_out,
       and_60_out, and_61_out, and_62_out, and_63_out, cpu_decoder_2x4_1__0, cpu_decoder_2x4_1__1,
       cpu_decoder_2x4_1__2, cpu_decoder_2x4_1__3, cpu_decoder_2x4_west_1__0, cpu_decoder_2x4_west_1__1,
       cpu_decoder_2x4_west_1__2, cpu_decoder_2x4_west_1__3, cpu_decoder_2x4_west_2__0,
       cpu_decoder_2x4_west_2__1, cpu_decoder_2x4_west_2__2, cpu_decoder_2x4_west_2__3,
       cpu_decoder_cntrl_3x8_1__0, cpu_decoder_cntrl_3x8_1__1, cpu_decoder_cntrl_3x8_1__2,
       cpu_decoder_cntrl_3x8_1__3, cpu_decoder_cntrl_3x8_1__4, cpu_decoder_cntrl_3x8_1__5,
       cpu_decoder_cntrl_3x8_1__6, cpu_decoder_cntrl_3x8_1__7, cpu_stepper_1_step_1, cpu_stepper_1_step_2,
       cpu_stepper_1_step_3, cpu_stepper_1_step_4, cpu_stepper_1_step_5, cpu_stepper_1_step_6,
       cpu_stepper_1_step_7, not_1_out, not_2_out, not_3_out, not_4_out, not_5_out, not_6_out, not_7_out,
       or_6_out, or_7_out, or_8_out, or_9_out, or_10_out, or_11_out, or_12_out, or_13_out, or_14_out,
       or_15_out, or_16_out;

  and and_1 (IAR_E, clke, or_6_out);
  and and_2 (RAM_E, clke, or_7_out);
  and and_3 (ACC_E, clke, or_8_out);
  and and_4 (IO_CLK_E, clke, and_47_out);
  or or_1 (R0_E, and_5_out, and_9_out);
  or or_2 (R1_E, and_6_out, and_10_out);
  or or_3 (R2_E, and_7_out, and_11_out);
  or or_4 (R3_E, and_8_out, and_12_out);
  and and_5 (and_5_out, clke, or_9_out, cpu_decoder_2x4_west_1__0);
  and and_6 (and_6_out, clke, or_9_out, cpu_decoder_2x4_west_1__1);
  and and_7 (and_7_out, clke, or_9_out, cpu_decoder_2x4_west_1__2);
  and and_8 (and_8_out, clke, or_9_out, cpu_decoder_2x4_west_1__3);
  and and_9 (and_9_out, clke, or_10_out, cpu_decoder_2x4_west_2__0);
  and and_10 (and_10_out, clke, or_10_out, cpu_decoder_2x4_west_2__1);
  and and_11 (and_11_out, clke, or_10_out, cpu_decoder_2x4_west_2__2);
  and and_12 (and_12_out, clke, or_10_out, cpu_decoder_2x4_west_2__3);
  and and_13 (ALU_0, cpu_stepper_1_step_5, IR_IN[7], IR_IN[4]);
  and and_14 (ALU_1, cpu_stepper_1_step_5, IR_IN[7], IR_IN[5]);
  and and_15 (ALU_2, cpu_stepper_1_step_5, IR_IN[7], IR_IN[6]);
  or or_5 (BUS_1, and_17_out, and_38_out, and_37_out, and_34_out);
  or or_6 (or_6_out, and_17_out, and_34_out, and_36_out, and_37_out);
  or or_7 (or_7_out, cpu_stepper_1_step_2, and_50_out, and_45_out, and_44_out, and_42_out);
  or or_8 (or_8_out, cpu_stepper_1_step_3, and_46_out, and_49_out, and_48_out);
  or or_9 (or_9_out, and_31_out, and_43_out, and_35_out, and_39_out);
  or or_10 (or_10_out, and_33_out, and_32_out, C_2);
  and and_16 (and_16_out, clk, not_1_out);
  not not_1 (not_1_out, LOAD);
  not not_2 (not_2_out, LOAD);
  CPU_DECODER_2x4_WEST cpu_decoder_2x4_west_1 (
    .a(IR_IN[0]), .b(IR_IN[1]), ._0(cpu_decoder_2x4_west_1__0), ._1(cpu_decoder_2x4_west_1__1),
    ._2(cpu_decoder_2x4_west_1__2), ._3(cpu_decoder_2x4_west_1__3));
  CPU_DECODER_2x4_WEST cpu_decoder_2x4_west_2 (
    .a(IR_IN[2]), .b(IR_IN[3]), ._0(cpu_decoder_2x4_west_2__0), ._1(cpu_decoder_2x4_west_2__1),
    ._2(cpu_decoder_2x4_west_2__2), ._3(cpu_decoder_2x4_west_2__3));
  CPU_STEPPER cpu_stepper_1 (
    .step_1(cpu_stepper_1_step_1), .step_2(cpu_stepper_1_step_2), .step_3(cpu_stepper_1_step_3),
    .step_4(cpu_stepper_1_step_4), .step_5(cpu_stepper_1_step_5), .step_6(cpu_stepper_1_step_6),
    .step_7(cpu_stepper_1_step_7), .reset(cpu_stepper_1_step_7), .clk(and_16_out));
  and and_17 (and_17_out, not_2_out, cpu_stepper_1_step_1);
  not not_3 (not_3_out, IR_IN[7]);
  CPU_DECODER_CNTRL_3x8 cpu_decoder_cntrl_3x8_1 (
    .a(IR_IN[6]), .b(IR_IN[5]), .c(IR_IN[4]), ._0(cpu_decoder_cntrl_3x8_1__0),
    ._1(cpu_decoder_cntrl_3x8_1__1), ._2(cpu_decoder_cntrl_3x8_1__2), ._3(cpu_decoder_cntrl_3x8_1__3),
    ._4(cpu_decoder_cntrl_3x8_1__4), ._5(cpu_decoder_cntrl_3x8_1__5), ._6(cpu_decoder_cntrl_3x8_1__6),
    ._7(cpu_decoder_cntrl_3x8_1__7));
  and and_18 (and_18_out, not_3_out, cpu_decoder_cntrl_3x8_1__0);
  and and_19 (and_19_out, not_3_out, cpu_decoder_cntrl_3x8_1__1);
  and and_20 (and_20_out, not_3_out, cpu_decoder_cntrl_3x8_1__2);
  and and_21 (and_21_out, not_3_out, cpu_decoder_cntrl_3x8_1__3);
  and and_22 (and_22_out, not_3_out, cpu_decoder_cntrl_3x8_1__4);
  and and_23 (and_23_out, not_3_out, cpu_decoder_cntrl_3x8_1__5);
  and and_24 (and_24_out, not_3_out, cpu_decoder_cntrl_3x8_1__6);
  and and_25 (and_25_out, not_3_out, cpu_decoder_cntrl_3x8_1__7);
  not not_4 (not_4_out, IR_IN[5]);
  not not_5 (not_5_out, IR_IN[4]);
  and and_26 (and_26_out, C, IR_IN[3]);
  and and_27 (and_27_out, A, IR_IN[2]);
  and and_28 (and_28_out, E, IR_IN[1]);
  and and_29 (and_29_out, Z, IR_IN[0]);
  or or_11 (or_11_out, and_26_out, and_27_out, and_28_out, and_29_out);
  and and_30 (and_30_out, IR_IN[4], IR_IN[5], IR_IN[6]);
  not not_6 (not_6_out, and_30_out);
  and and_31 (and_31_out, cpu_stepper_1_step_4, IR_IN[7]);
  and and_32 (and_32_out, cpu_stepper_1_step_4, and_18_out);
  and and_33 (and_33_out, cpu_stepper_1_step_4, and_19_out);
  and and_34 (and_34_out, cpu_stepper_1_step_4, and_20_out);
  and and_35 (and_35_out, cpu_stepper_1_step_4, and_21_out);
  and and_36 (and_36_out, cpu_stepper_1_step_4, and_22_out);
  and and_37 (and_37_out, cpu_stepper_1_step_4, and_23_out);
  and and_38 (and_38_out, cpu_stepper_1_step_4, and_24_out);
  and and_39 (and_39_out, cpu_stepper_1_step_4, and_25_out, IR_IN[3]);
  and and_40 (END, IR_IN[7], IR_IN[6], not_4_out, not_5_out, cpu_stepper_1_step_4, IR_IN[3], IR_IN[2], IR_IN[1], IR_IN[0]);
  and and_41 (C_2, cpu_stepper_1_step_5, IR_IN[7]);
  and and_42 (and_42_out, cpu_stepper_1_step_5, and_18_out);
  and and_43 (and_43_out, cpu_stepper_1_step_5, and_19_out);
  and and_44 (and_44_out, cpu_stepper_1_step_5, and_20_out);
  and and_45 (and_45_out, cpu_stepper_1_step_5, and_22_out);
  and and_46 (and_46_out, cpu_stepper_1_step_5, and_23_out);
  not not_7 (not_7_out, IR_IN[3]);
  and and_47 (and_47_out, cpu_stepper_1_step_5, and_25_out, not_7_out);
  and and_48 (and_48_out, cpu_stepper_1_step_6, IR_IN[7], not_6_out);
  and and_49 (and_49_out, cpu_stepper_1_step_6, and_20_out);
  and and_50 (and_50_out, cpu_stepper_1_step_6, and_23_out, or_11_out);
  CPU_DECODER_2x4 cpu_decoder_2x4_1 (
    .a(IR_IN[0]), .b(IR_IN[1]), ._0(cpu_decoder_2x4_1__0), ._1(cpu_decoder_2x4_1__1),
    ._2(cpu_decoder_2x4_1__2), ._3(cpu_decoder_2x4_1__3));
  or or_12 (or_12_out, and_17_out, and_34_out, and_37_out, and_32_out, and_33_out, and_36_out);
  or or_13 (or_13_out, cpu_stepper_1_step_3, and_35_out, and_46_out, and_45_out, and_49_out, and_50_out);
  or or_14 (or_14_out, and_17_out, and_34_out, and_37_out, C_2);
  or or_15 (or_15_out, and_38_out, C_2);
  or or_16 (or_16_out, and_42_out, and_48_out, and_44_out, and_47_out);
  and and_51 (and_51_out, clks, cpu_stepper_1_step_2);
  and and_52 (and_52_out, clks, or_12_out);
  and and_53 (and_53_out, clks, or_13_out);
  and and_54 (and_54_out, clks, or_14_out);
  and and_55 (and_55_out, LOAD, clks);
  and and_56 (and_56_out, clks, and_43_out);
  and and_57 (and_57_out, clks, and_31_out);
  and and_58 (and_58_out, clks, or_15_out);
  and and_59 (IO_CLKS_S, clks, and_39_out);
  and and_60 (and_60_out, clks, or_16_out, cpu_decoder_2x4_1__0);
  and and_61 (and_61_out, clks, or_16_out, cpu_decoder_2x4_1__1);
  and and_62 (and_62_out, clks, or_16_out, cpu_decoder_2x4_1__2);
  and and_63 (and_63_out, clks, or_16_out, cpu_decoder_2x4_1__3);
  or or_17 (IR_S, RESET, and_51_out);
  or or_18 (MAR_S, MARS, and_52_out);
  or or_19 (IAR_S, RESET, and_53_out);
  or or_20 (ACC_S, RESET, and_54_out);
  or or_21 (RAM_S, and_55_out, and_56_out);
  or or_22 (TMP_S, RESET, and_57_out);
  or or_23 (FLAGS_S, RESET, and_58_out);
  or or_24 (R0_S, RESET, and_60_out);
  or or_25 (R1_S, RESET, and_61_out);
  or or_26 (R2_S, RESET, and_62_out);
  or or_27 (R3_S, RESET, and_63_out);

  assign DA = IR_IN[3];
  assign IO = IR_IN[2];

  // Notes on the sheet:
  //   REG B_E
  //   REG A
  //   REG B
  //   REG A
  //   REG B_S
endmodule

module CPU_CLK (
  input  clkin,
  output clk,
  output clks,
  output clke
);

  wire j_k_ff_1_qn, nand_1_out;

  J_K_Flip_Flop j_k_ff_1 (.J(1'b1), .clk(clkin), .K(1'b1), .Q(clk), .Qn(j_k_ff_1_qn));  // open: preset, en, reset
  nand nand_1 (nand_1_out, clkin, clk);
  nand nand_2 (clke, j_k_ff_1_qn, clkin);
  not not_1 (clks, nand_1_out);

  // Notes on the sheet:
  //   clk: pull=down
  //   clke: pull=down
  //   clkin: pull=down
  //   clks: pull=down
endmodule

module CPU_DECODER_2x4 (
  input  a,
  input  b,
  output _0,
  output _1,
  output _2,
  output _3
);

  wire not_1_out, not_2_out;

  not not_1 (not_1_out, b);
  not not_2 (not_2_out, a);
  and and_1 (_0, not_2_out, not_1_out);
  and and_2 (_1, a, not_1_out);
  and and_3 (_2, b, not_2_out);
  and and_4 (_3, b, a);

  // Notes on the sheet:
  //   b: pull=down
  //   a: pull=down
endmodule

module CPU_DECODER_2x4_WEST (
  input  a,
  input  b,
  output _0,
  output _1,
  output _2,
  output _3
);

  wire not_1_out, not_2_out;

  not not_1 (not_1_out, b);
  not not_2 (not_2_out, a);
  and and_1 (_0, not_2_out, not_1_out);
  and and_2 (_1, a, not_1_out);
  and and_3 (_2, b, not_2_out);
  and and_4 (_3, b, a);

  // Notes on the sheet:
  //   b: pull=down
  //   a: pull=down
endmodule

module CPU_DECODER_CNTRL_3x8 (
  input  a,
  input  b,
  input  c,
  output _0,
  output _1,
  output _2,
  output _3,
  output _4,
  output _5,
  output _6,
  output _7
);

  wire not_1_out, not_2_out, not_3_out;

  not not_1 (not_1_out, c);
  not not_2 (not_2_out, b);
  not not_3 (not_3_out, a);
  and and_1 (_0, not_3_out, not_2_out, not_1_out);
  and and_2 (_1, not_3_out, not_2_out, c);
  and and_3 (_2, not_3_out, b, not_1_out);
  and and_4 (_3, not_3_out, b, c);
  and and_5 (_4, a, not_2_out, not_1_out);
  and and_6 (_5, a, not_2_out, c);
  and and_7 (_6, a, b, not_1_out);
  and and_8 (_7, a, b, c);

  // Notes on the sheet:
  //   c: pull=down
  //   b: pull=down
  //   a: pull=down
endmodule

module CPU_TEST (
  input  LOAD,
  input  MARS
);

  wire CLK, CLKE, CLKL, CLKS, END, RESET;
  wire [7:0] ACC, BUS, IAR, IR, load_256_count_1_count, R0, R1, R2, R3, RAM_INPUT;

  Hex_Digit_Display hex_digit_display_1 (.value(BUS[7:4]));  // open: dp
  CPU cpu_1 (
    .LOAD(LOAD), .RAM_INPUT(RAM_INPUT), .RESET(RESET), .BUS_OUTPUT(BUS), .R0(R0), .R1(R1), .R2(R2), .R3(R3),
    .out_18(IR), .out_19(IAR), .clock(CLK), .clkl(CLKL), .out_20(ACC), .MARS(MARS), .END(END), .clks(CLKS),
    .clke(CLKE));  // open: S, E, IO, DA
  Hex_Digit_Display hex_digit_display_2 (.value(BUS[3:0]));  // open: dp
  LOAD_256_COUNT load_256_count_1 (.count(load_256_count_1_count), .clk(CLKL));  // open: carry
  Hex_Digit_Display hex_digit_display_3 (.value(ACC[7:4]));  // open: dp
  Hex_Digit_Display hex_digit_display_4 (.value(ACC[3:0]));  // open: dp
  RAM ram_1 (.addr(load_256_count_1_count), .data(RAM_INPUT), .sel(LOAD), .clk(CLKL), .ld(1'b1), .clr(1'b0));
  Hex_Digit_Display hex_digit_display_5 (.value(IAR[3:0]));  // open: dp
  Hex_Digit_Display hex_digit_display_6 (.value(IAR[7:4]));  // open: dp
  Hex_Digit_Display hex_digit_display_7 (.value(IR[7:4]));  // open: dp
  Hex_Digit_Display hex_digit_display_8 (.value(IR[3:0]));  // open: dp
  Hex_Digit_Display hex_digit_display_9 (.value(R0[7:4]));  // open: dp
  Hex_Digit_Display hex_digit_display_10 (.value(R0[3:0]));  // open: dp
  Hex_Digit_Display hex_digit_display_11 (.value(R1[3:0]));  // open: dp
  Hex_Digit_Display hex_digit_display_12 (.value(R1[7:4]));  // open: dp
  Button u_RESET (.out(RESET));
  LED #(.active("false")) led_1 (.in(END));
  Clock u_CLK (.out(CLK));
  Hex_Digit_Display hex_digit_display_13 (.value(R2[3:0]));  // open: dp
  Hex_Digit_Display hex_digit_display_14 (.value(R2[7:4]));  // open: dp
  Hex_Digit_Display hex_digit_display_15 (.value(R3[7:4]));  // open: dp
  Hex_Digit_Display hex_digit_display_16 (.value(R3[3:0]));  // open: dp

  // Notes on the sheet:
  //   BUS
  //   ACC
  //   EXTERNAL RAM
  //   IAR
  //   IR
  //   RO
  //   1 -
  //   2 -
  //   3 -
  //   0
  //   1
  //   0
  //   R1
  //   R2
  //   R3
endmodule

module CPU_CARRY_TEMP (
  input  c,
  input  s,
  output o
);

  CPU_MEM_1 cpu_mem_1_1 (.in_1(c), .in_2(s), .out_3(o));
endmodule

module LOAD_256_COUNT (
  input  clk,
  output [7:0] count,
  output carry
);

  wire counter_1_carry;

  Counter #(.ongoal("stay"), .trigger("falling")) counter_1 (
    .count(1'b1), .Q(count), .carry(counter_1_carry), .clk(clk));  // open: load, D, clr
  not not_1 (carry, counter_1_carry);
endmodule

module CPU_DELAY (
  input  [7:0] i,
  input  clk,
  output [7:0] o
);

  Counter #(.ongoal("stay"), .trigger("falling")) counter_1 (
    .load(1'b1), .D(i), .count(1'b0), .Q(o), .clk(clk));  // open: carry, clr
endmodule
